// Logisim project logi7400ic.circ as structural Verilog: 50 circuits, main circuit README
module README (
);

  // IC_7400 ic_7400_1: pin names not known
  // IC_7414 ic_7414_1: pin names not known
  // IC_7473 ic_7473_1: pin names not known
  // IC_74109 ic_74109_1: pin names not known
  // IC_74157 ic_74157_1: pin names not known
  // IC_74374 ic_74374_1: pin names not known
  // IC_7402 ic_7402_1: pin names not known
  // IC_7420 ic_7420_1: pin names not known
  // IC_7474 ic_7474_1: pin names not known
  // IC_74112 ic_74112_1: pin names not known
  // IC_74161 ic_74161_1: pin names not known
  // IC_74377 ic_74377_1: pin names not known
  // IC_7403 ic_7403_1: pin names not known
  // IC_7421 ic_7421_1: pin names not known
  // IC_7475 ic_7475_1: pin names not known
  // IC_74132 ic_74132_1: pin names not known
  // IC_74163 ic_74163_1: pin names not known
  // IC_74373 ic_74373_1: pin names not known
  // IC_7404 ic_7404_1: pin names not known
  // IC_7427 ic_7427_1: pin names not known
  // IC_7476 ic_7476_1: pin names not known
  // IC_74138 ic_74138_1: pin names not known
  // IC_74173 ic_74173_1: pin names not known
  // IC_74533 ic_74533_1: pin names not known
  // IC_7405 ic_7405_1: pin names not known
  // IC_7430 ic_7430_1: pin names not known
  // IC_7485 ic_7485_1: pin names not known
  // IC_74240 ic_74240_1: pin names not known
  // IC_74139 ic_74139_1: pin names not known
  // IC_74175 ic_74175_1: pin names not known
  // IC_7408 ic_7408_1: pin names not known
  // IC_7432 ic_7432_1: pin names not known
  // IC_7486 ic_7486_1: pin names not known
  // IC_74147 ic_74147_1: pin names not known
  // IC_74238 ic_74238_1: pin names not known
  // IC_7410 ic_7410_1: pin names not known
  // IC_7442 ic_7442_1: pin names not known
  // IC_7493 ic_7493_1: pin names not known
  // IC_74151 ic_74151_1: pin names not known
  // IC_74244 ic_74244_1: pin names not known
  // IC_7411 ic_7411_1: pin names not known
  // IC_7451 ic_7451_1: pin names not known
  // IC_74107 ic_74107_1: pin names not known
  // IC_74153 ic_74153_1: pin names not known
  // IC_74273 ic_74273_1: pin names not known
  // IC_74283 ic_74283_1: pin names not known

  // Notes on the sheet:
  //   Logisim 7400 series integrated circuits library
  //   Copyright (C) 2015 - 2018 by Stefan Rothe
  //   This library is licenced under the GNU Lesser General Public Licence version 3.
endmodule

module IC_7400 (
  input  A1,
  input  A2,
  input  A3,
  input  A4,
  input  B1,
  input  B2,
  input  B3,
  input  B4,
  output Y1,
  output Y2,
  output Y3,
  output Y4
);

  nand nand_1 (Y1, A1, B1);
  nand nand_2 (Y2, A2, B2);
  nand nand_3 (Y3, A3, B3);
  nand nand_4 (Y4, A4, B4);
endmodule

module IC_7402 (
  input  A1,
  input  A2,
  input  A3,
  input  A4,
  input  B1,
  input  B2,
  input  B3,
  input  B4,
  output Y1,
  output Y2,
  output Y3,
  output Y4
);

  nor nor_1 (Y1, A1, B1);
  nor nor_2 (Y2, A2, B2);
  nor nor_3 (Y3, A3, B3);
  nor nor_4 (Y4, A4, B4);
endmodule

module IC_7403 (
  input  A1,
  input  A2,
  input  A3,
  input  A4,
  input  B1,
  input  B2,
  input  B3,
  input  B4,
  output Y1,
  output Y2,
  output Y3,
  output Y4
);

  wire and_1_out, and_2_out, and_3_out, and_4_out;

  assign Y1 = and_1_out ? 1'b0 : 1'bz;  // Controlled_Buffer controlled_buffer_1
  and and_1 (and_1_out, A1, B1);
  assign Y2 = and_2_out ? 1'b0 : 1'bz;  // Controlled_Buffer controlled_buffer_2
  and and_2 (and_2_out, A2, B2);
  assign Y3 = and_3_out ? 1'b0 : 1'bz;  // Controlled_Buffer controlled_buffer_3
  and and_3 (and_3_out, A3, B3);
  assign Y4 = and_4_out ? 1'b0 : 1'bz;  // Controlled_Buffer controlled_buffer_4
  and and_4 (and_4_out, A4, B4);
endmodule

module IC_7404 (
  input  A1,
  input  A2,
  input  A3,
  input  A4,
  input  A5,
  input  A6,
  output Y1,
  output Y2,
  output Y3,
  output Y4,
  output Y5,
  output Y6
);

  not not_1 (Y1, A1);
  not not_2 (Y2, A2);
  not not_3 (Y3, A3);
  not not_4 (Y4, A4);
  not not_5 (Y5, A5);
  not not_6 (Y6, A6);
endmodule

module IC_7405 (
  input  A1,
  input  A2,
  input  A3,
  input  A4,
  input  A5,
  input  A6,
  output Y1,
  output Y2,
  output Y3,
  output Y4,
  output Y5,
  output Y6
);

  assign Y1 = A1 ? 1'b0 : 1'bz;  // Controlled_Buffer controlled_buffer_1
  assign Y2 = A2 ? 1'b0 : 1'bz;  // Controlled_Buffer controlled_buffer_2
  assign Y3 = A3 ? 1'b0 : 1'bz;  // Controlled_Buffer controlled_buffer_3
  assign Y4 = A4 ? 1'b0 : 1'bz;  // Controlled_Buffer controlled_buffer_4
  assign Y5 = A5 ? 1'b0 : 1'bz;  // Controlled_Buffer controlled_buffer_5
  assign Y6 = A6 ? 1'b0 : 1'bz;  // Controlled_Buffer controlled_buffer_6
endmodule

module IC_7408 (
  input  A1,
  input  A2,
  input  A3,
  input  A4,
  input  B1,
  input  B2,
  input  B3,
  input  B4,
  output Y1,
  output Y2,
  output Y3,
  output Y4
);

  and and_1 (Y1, A1, B1);
  and and_2 (Y2, A2, B2);
  and and_3 (Y3, A3, B3);
  and and_4 (Y4, A4, B4);
endmodule

module IC_7410 (
  input  A1,
  input  A2,
  input  A3,
  input  B1,
  input  B2,
  input  B3,
  input  C1,
  input  C2,
  input  C3,
  output Y1,
  output Y2,
  output Y3
);

  nand nand_1 (Y1, A1, B1, C1);
  nand nand_2 (Y2, A2, B2, C2);
  nand nand_3 (Y3, A3, B3, C3);
endmodule

module IC_7411 (
  input  A1,
  input  A2,
  input  A3,
  input  B1,
  input  B2,
  input  B3,
  input  C1,
  input  C2,
  input  C3,
  output Y1,
  output Y2,
  output Y3
);

  and and_1 (Y1, A1, B1, C1);
  and and_2 (Y2, A2, B2, C2);
  and and_3 (Y3, A3, B3, C3);
endmodule

module IC_7414 (
  input  A1,
  input  A2,
  input  A3,
  input  A4,
  input  A5,
  input  A6,
  output Y1,
  output Y2,
  output Y3,
  output Y4,
  output Y5,
  output Y6
);

  not not_1 (Y1, A1);
  not not_2 (Y2, A2);
  not not_3 (Y3, A3);
  not not_4 (Y4, A4);
  not not_5 (Y5, A5);
  not not_6 (Y6, A6);
endmodule

module IC_7420 (
  input  A1,
  input  A2,
  input  B1,
  input  B2,
  input  C1,
  input  C2,
  input  D1,
  input  D2,
  output Y1,
  output Y2
);

  nand nand_1 (Y1, A1, B1, C1, D1);
  nand nand_2 (Y2, A2, B2, C2, D2);
endmodule

module IC_7421 (
  input  A1,
  input  A2,
  input  B1,
  input  B2,
  input  C1,
  input  C2,
  input  D1,
  input  D2,
  output Y1,
  output Y2
);

  and and_1 (Y1, A1, B1, C1, D1);
  and and_2 (Y2, A2, B2, C2, D2);
endmodule

module IC_7427 (
  input  A1,
  input  A2,
  input  A3,
  input  B1,
  input  B2,
  input  B3,
  input  C1,
  input  C2,
  input  C3,
  output Y1,
  output Y2,
  output Y3
);

  nor nor_1 (Y1, A1, B1, C1);
  nor nor_2 (Y2, A2, B2, C2);
  nor nor_3 (Y3, A3, B3, C3);
endmodule

module IC_7430 (
  input  A,
  input  B,
  input  C,
  input  D,
  input  E,
  input  F,
  input  G,
  input  H,
  output Y
);

  nand nand_1 (Y, A, B, C, D, E, F, G, H);
endmodule

module IC_7432 (
  input  A1,
  input  A2,
  input  A3,
  input  A4,
  input  B1,
  input  B2,
  input  B3,
  input  B4,
  output Y1,
  output Y2,
  output Y3,
  output Y4
);

  or or_1 (Y1, A1, B1);
  or or_2 (Y2, A2, B2);
  or or_3 (Y3, A3, B3);
  or or_4 (Y4, A4, B4);
endmodule

module IC_7442 (
  input  D1,
  input  D2,
  input  D3,
  input  D4,
  output Y0,
  output Y1,
  output Y2,
  output Y3,
  output Y4,
  output Y5,
  output Y6,
  output Y7,
  output Y8,
  output Y9
);

  wire nand_1_out, nand_2_out, nand_3_out, nand_4_out, nand_5_out, nand_6_out, nand_7_out, not_1_out,
       not_2_out, not_3_out, not_4_out, not_5_out, not_6_out, not_7_out, not_8_out;

  not not_1 (not_1_out, D1);
  not not_2 (not_2_out, D2);
  not not_3 (not_3_out, D3);
  not not_4 (not_4_out, D4);
  not not_5 (not_5_out, not_1_out);
  not not_6 (not_6_out, not_2_out);
  not not_7 (not_7_out, not_3_out);
  not not_8 (not_8_out, not_4_out);
  nand nand_1 (nand_1_out, not_1_out, not_2_out);
  nand nand_2 (nand_2_out, not_5_out, not_2_out);
  nand nand_3 (nand_3_out, not_1_out, not_6_out);
  nand nand_4 (nand_4_out, not_5_out, not_6_out);
  nand nand_5 (nand_5_out, not_3_out, not_4_out);
  nand nand_6 (nand_6_out, not_7_out, not_4_out);
  nand nand_7 (nand_7_out, not_3_out, not_8_out);
  nand nand_8 (Y0, ~nand_1_out, ~nand_5_out);  // NAND_Gate
  nand nand_9 (Y1, ~nand_2_out, ~nand_5_out);  // NAND_Gate
  nand nand_10 (Y2, ~nand_3_out, ~nand_5_out);  // NAND_Gate
  nand nand_11 (Y3, ~nand_4_out, ~nand_5_out);  // NAND_Gate
  nand nand_12 (Y4, ~nand_1_out, ~nand_6_out);  // NAND_Gate
  nand nand_13 (Y5, ~nand_2_out, ~nand_6_out);  // NAND_Gate
  nand nand_14 (Y6, ~nand_3_out, ~nand_6_out);  // NAND_Gate
  nand nand_15 (Y7, ~nand_4_out, ~nand_6_out);  // NAND_Gate
  nand nand_16 (Y8, ~nand_1_out, ~nand_7_out);  // NAND_Gate
  nand nand_17 (Y9, ~nand_2_out, ~nand_7_out);  // NAND_Gate
endmodule

module IC_7451 (
  input  A1,
  input  B1,
  input  C1,
  input  D1,
  input  E1,
  input  F1,
  input  A2,
  input  B2,
  input  C2,
  input  D2,
  output Y1,
  output Y2
);

  wire and_1_out, and_2_out, and_3_out, and_4_out;

  and and_1 (and_1_out, A1, B1, C1);
  and and_2 (and_2_out, D1, E1, F1);
  and and_3 (and_3_out, A2, B2);
  and and_4 (and_4_out, C2, D2);
  nor nor_1 (Y1, and_1_out, and_2_out);
  nor nor_2 (Y2, and_3_out, and_4_out);
endmodule

module IC_7473 (
  input  J1,
  input  CLK1,
  input  K1,
  input  CLR1,
  input  J2,
  input  CLK2,
  input  K2,
  input  CLR2,
  output Q1,
  output R1,
  output Q2,
  output R2
);

  wire not_1_out, not_2_out, not_3_out, not_4_out;

  not not_1 (not_1_out, CLK1);
  not not_2 (not_2_out, CLR1);
  not not_3 (not_3_out, CLK2);
  not not_4 (not_4_out, CLR2);
  JK_Flip_Flop jk_flip_flop_1 (.R(R1), .Q(Q1), .CLR(not_2_out), .CLK(not_1_out), .K(K1), .J(J1));  // open: SET
  JK_Flip_Flop jk_flip_flop_2 (.R(R2), .Q(Q2), .CLR(not_4_out), .CLK(not_3_out), .K(K2), .J(J2));  // open: SET
endmodule

module IC_7474 (
  input  SET1,
  input  D1,
  input  CLK1,
  input  CLR1,
  input  SET2,
  input  D2,
  input  CLK2,
  input  CLR2,
  output Q1,
  output R1,
  output Q2,
  output R2
);

  wire not_1_out, not_2_out, not_3_out, not_4_out;

  not not_1 (not_1_out, SET1);
  D_Flip_Flop d_flip_flop_1 (.Q(Q1), .R(R1), .SET(not_1_out), .CLR(not_2_out), .D(D1), .CLK(CLK1));
  not not_2 (not_2_out, CLR1);
  not not_3 (not_3_out, SET2);
  D_Flip_Flop d_flip_flop_2 (.Q(Q2), .R(R2), .SET(not_3_out), .CLR(not_4_out), .D(D2), .CLK(CLK2));
  not not_4 (not_4_out, CLR2);
endmodule

module IC_7475 (
  input  D1,
  input  D2,
  input  LE12,
  input  D3,
  input  D4,
  input  LE34,
  output Q1,
  output R1,
  output Q2,
  output R2,
  output Q3,
  output R3,
  output Q4,
  output R4
);

  D_Latch d_latch_1 (.Q(Q1), .R(R1), .D(D1), .LE(LE12));  // open: SET, CLR
  D_Latch d_latch_2 (.Q(Q2), .R(R2), .D(D2), .LE(LE12));  // open: SET, CLR
  D_Latch d_latch_3 (.Q(Q3), .R(R3), .D(D3), .LE(LE34));  // open: SET, CLR
  D_Latch d_latch_4 (.Q(Q4), .R(R4), .D(D4), .LE(LE34));  // open: SET, CLR
endmodule

module IC_7476 (
  input  SET1,
  input  J1,
  input  CLK1,
  input  K1,
  input  CLR1,
  input  SET2,
  input  J2,
  input  CLK2,
  input  K2,
  input  CLR2,
  output Q1,
  output R1,
  output Q2,
  output R2
);

  wire not_1_out, not_2_out, not_3_out, not_4_out, not_5_out, not_6_out;

  not not_1 (not_1_out, SET1);
  not not_2 (not_2_out, CLK1);
  not not_3 (not_3_out, CLR1);
  not not_4 (not_4_out, SET2);
  not not_5 (not_5_out, CLK2);
  not not_6 (not_6_out, CLR2);
  JK_Flip_Flop jk_flip_flop_1 (.R(R1), .Q(Q1), .CLR(not_3_out), .SET(not_1_out), .CLK(not_2_out), .K(K1), .J(J1));
  JK_Flip_Flop jk_flip_flop_2 (.R(R2), .Q(Q2), .CLR(not_6_out), .SET(not_4_out), .CLK(not_5_out), .K(K2), .J(J2));
endmodule

module IC_7485 (
  input  A1,
  input  A2,
  input  A3,
  input  A4,
  input  B1,
  input  B2,
  input  B3,
  input  B4,
  input  CLT,
  input  CEQ,
  input  CGT,
  output YLT,
  output YEQ,
  output YGT
);

  wire and_1_out, and_2_out, and_3_out, and_4_out, and_5_out, and_6_out, and_7_out, and_8_out, and_9_out,
       and_10_out, and_11_out, and_12_out, and_13_out, and_14_out, and_16_out, and_17_out, and_18_out,
       and_19_out, and_20_out, and_21_out, nand_1_out, nand_2_out, nand_3_out, nand_4_out, nor_1_out,
       nor_2_out, nor_3_out, nor_4_out;

  nand nand_1 (nand_1_out, A4, B4);
  nand nand_2 (nand_2_out, A3, B3);
  nand nand_3 (nand_3_out, A2, B2);
  nand nand_4 (nand_4_out, A1, B1);
  and and_1 (and_1_out, A4, nand_1_out);
  and and_2 (and_2_out, nand_1_out, B4);
  and and_3 (and_3_out, A3, nand_2_out);
  and and_4 (and_4_out, nand_2_out, B3);
  and and_5 (and_5_out, A2, nand_3_out);
  and and_6 (and_6_out, nand_3_out, B2);
  and and_7 (and_7_out, A1, nand_4_out);
  and and_8 (and_8_out, nand_4_out, B1);
  nor nor_1 (nor_1_out, and_1_out, and_2_out);
  nor nor_2 (nor_2_out, and_3_out, and_4_out);
  nor nor_3 (nor_3_out, and_5_out, and_6_out);
  nor nor_4 (nor_4_out, and_7_out, and_8_out);
  and and_9 (and_9_out, B4, nand_1_out);
  and and_10 (and_10_out, B3, nand_2_out, nor_1_out);
  and and_11 (and_11_out, B2, nand_3_out, nor_1_out, nor_2_out);
  and and_12 (and_12_out, B1, nand_4_out, nor_1_out, nor_2_out, nor_3_out);
  and and_13 (and_13_out, nor_1_out, nor_2_out, nor_3_out, nor_4_out, CLT);
  and and_14 (and_14_out, nor_1_out, nor_2_out, nor_3_out, nor_4_out, CEQ);
  and and_15 (YEQ, nor_1_out, nor_2_out, CEQ, nor_3_out, nor_4_out);
  and and_16 (and_16_out, CEQ, nor_4_out, nor_3_out, nor_2_out, nor_1_out);
  and and_17 (and_17_out, CGT, nor_4_out, nor_3_out, nor_2_out, nor_1_out);
  and and_18 (and_18_out, nor_3_out, nor_2_out, nor_1_out, nand_4_out, A1);
  and and_19 (and_19_out, nor_2_out, nor_1_out, nand_3_out, A2);
  and and_20 (and_20_out, nor_1_out, nand_2_out, A3);
  and and_21 (and_21_out, nand_1_out, A4);
  nor nor_5 (YGT, and_9_out, and_10_out, and_11_out, and_12_out, and_13_out, and_14_out);
  nor nor_6 (YLT, and_16_out, and_17_out, and_18_out, and_19_out, and_20_out, and_21_out);
endmodule

module IC_7486 (
  input  A1,
  input  A2,
  input  A3,
  input  A4,
  input  B1,
  input  B2,
  input  B3,
  input  B4,
  output Y1,
  output Y2,
  output Y3,
  output Y4
);

  xor xor_1 (Y1, A1, B1);
  xor xor_2 (Y2, A2, B2);
  xor xor_3 (Y3, A3, B3);
  xor xor_4 (Y4, A4, B4);
endmodule

module IC_7493 (
  input  CLK0,
  input  CLK1,
  input  CLR1,
  input  CLR2,
  output Q1,
  output Q2,
  output Q3,
  output Q4
);

  wire and_1_out, d_flip_flop_1_r, d_flip_flop_2_r, d_flip_flop_3_r, d_flip_flop_4_r, not_1_out, not_2_out,
       not_3_out, not_4_out;

  not not_1 (not_1_out, CLK0);
  not not_2 (not_2_out, CLK1);
  and and_1 (and_1_out, CLR1, CLR2);
  not not_3 (not_3_out, Q2);
  not not_4 (not_4_out, Q3);
  D_Flip_Flop d_flip_flop_1 (
    .Q(Q1), .R(d_flip_flop_1_r), .CLR(and_1_out), .D(d_flip_flop_1_r), .CLK(not_1_out));  // open: SET
  D_Flip_Flop d_flip_flop_2 (
    .Q(Q2), .R(d_flip_flop_2_r), .CLR(and_1_out), .D(d_flip_flop_2_r), .CLK(not_2_out));  // open: SET
  D_Flip_Flop d_flip_flop_3 (
    .Q(Q3), .R(d_flip_flop_3_r), .CLR(and_1_out), .D(d_flip_flop_3_r), .CLK(not_3_out));  // open: SET
  D_Flip_Flop d_flip_flop_4 (.Q(Q4), .R(d_flip_flop_4_r), .D(d_flip_flop_4_r), .CLK(not_4_out));  // open: SET, CLR
endmodule

module IC_74107 (
  input  J1,
  input  CLK1,
  input  K1,
  input  CLR1,
  input  J2,
  input  CLK2,
  input  K2,
  input  CLR2,
  output Q1,
  output R1,
  output Q2,
  output R2
);

  wire not_1_out, not_2_out, not_3_out, not_4_out;

  not not_1 (not_1_out, K1);
  not not_2 (not_2_out, CLR1);
  not not_3 (not_3_out, K2);
  not not_4 (not_4_out, CLR2);
  JK_Flip_Flop jk_flip_flop_1 (.R(R1), .Q(Q1), .CLR(not_2_out), .CLK(CLK1), .K(not_1_out), .J(J1));  // open: SET
  JK_Flip_Flop jk_flip_flop_2 (.R(R2), .Q(Q2), .CLR(not_4_out), .CLK(CLK2), .K(not_3_out), .J(J2));  // open: SET
endmodule

module IC_74109 (
  input  SET1,
  input  J1,
  input  CLK1,
  input  K1,
  input  CLR1,
  input  SET2,
  input  J2,
  input  CLK2,
  input  K2,
  input  CLR2,
  output Q1,
  output R1,
  output Q2,
  output R2
);

  wire not_1_out, not_2_out, not_3_out, not_4_out, not_5_out, not_6_out;

  not not_1 (not_1_out, SET1);
  not not_2 (not_2_out, K1);
  not not_3 (not_3_out, CLR1);
  not not_4 (not_4_out, SET2);
  not not_5 (not_5_out, K2);
  not not_6 (not_6_out, CLR2);
  JK_Flip_Flop jk_flip_flop_1 (.R(R1), .Q(Q1), .CLR(not_3_out), .SET(not_1_out), .CLK(CLK1), .K(not_2_out), .J(J1));
  JK_Flip_Flop jk_flip_flop_2 (.R(R2), .Q(Q2), .CLR(not_6_out), .SET(not_4_out), .CLK(CLK2), .K(not_5_out), .J(J2));
endmodule

module IC_74112 (
  input  SET1,
  input  J1,
  input  CLK1,
  input  K1,
  input  CLR1,
  input  SET2,
  input  J2,
  input  CLK2,
  input  K2,
  input  CLR2,
  output Q1,
  output R1,
  output Q2,
  output R2
);

  wire not_1_out, not_2_out, not_3_out, not_4_out, not_5_out, not_6_out;

  not not_1 (not_1_out, SET1);
  not not_2 (not_2_out, CLK1);
  not not_3 (not_3_out, CLR1);
  not not_4 (not_4_out, SET2);
  not not_5 (not_5_out, CLK2);
  not not_6 (not_6_out, CLR2);
  JK_Flip_Flop jk_flip_flop_1 (.R(R1), .Q(Q1), .CLR(not_3_out), .SET(not_1_out), .CLK(not_2_out), .K(K1), .J(J1));
  JK_Flip_Flop jk_flip_flop_2 (.R(R2), .Q(Q2), .CLR(not_6_out), .SET(not_4_out), .CLK(not_5_out), .K(K2), .J(J2));
endmodule

module IC_74132 (
  input  A1,
  input  A2,
  input  A3,
  input  A4,
  input  B1,
  input  B2,
  input  B3,
  input  B4,
  output Y1,
  output Y2,
  output Y3,
  output Y4
);

  nand nand_1 (Y1, A1, B1);
  nand nand_2 (Y2, A2, B2);
  nand nand_3 (Y3, A3, B3);
  nand nand_4 (Y4, A4, B4);
endmodule

module IC_74138 (
  input  A0,
  input  A1,
  input  A2,
  input  OE1,
  input  OE2,
  input  OE3,
  output Y0,
  output Y1,
  output Y2,
  output Y3,
  output Y4,
  output Y5,
  output Y6,
  output Y7
);

  wire and_1_out, not_1_out, not_2_out, not_3_out, not_4_out, not_5_out;

  not not_1 (not_1_out, A0);
  not not_2 (not_2_out, A1);
  not not_3 (not_3_out, A2);
  not not_4 (not_4_out, OE1);
  not not_5 (not_5_out, OE2);
  and and_1 (and_1_out, not_4_out, not_5_out, OE3);
  nand nand_1 (Y0, not_1_out, not_2_out, not_3_out, and_1_out);
  nand nand_2 (Y1, A0, not_2_out, not_3_out, and_1_out);
  nand nand_3 (Y2, not_1_out, A1, not_3_out, and_1_out);
  nand nand_4 (Y3, A0, A1, not_3_out, and_1_out);
  nand nand_5 (Y4, not_1_out, not_2_out, A2, and_1_out);
  nand nand_6 (Y5, A0, not_2_out, A2, and_1_out);
  nand nand_7 (Y6, not_1_out, A1, A2, and_1_out);
  nand nand_8 (Y7, A0, A1, A2, and_1_out);
endmodule

module IC_74139 (
  input  A0,
  input  A1,
  input  OEA,
  input  B0,
  input  B1,
  input  OEB,
  output Y0,
  output Y1,
  output Y2,
  output Y3,
  output Z0,
  output Z1,
  output Z2,
  output Z3
);

  wire not_1_out, not_2_out, not_3_out, not_4_out, not_5_out, not_6_out;

  not not_1 (not_1_out, A0);
  not not_2 (not_2_out, A1);
  not not_3 (not_3_out, OEA);
  not not_4 (not_4_out, B0);
  not not_5 (not_5_out, B1);
  not not_6 (not_6_out, OEB);
  nand nand_1 (Y0, not_1_out, not_2_out, not_3_out);
  nand nand_2 (Y1, A0, not_2_out, not_3_out);
  nand nand_3 (Y2, not_1_out, A1, not_3_out);
  nand nand_4 (Y3, A0, A1, not_3_out);
  nand nand_5 (Z0, not_4_out, not_5_out, not_6_out);
  nand nand_6 (Z1, B0, not_5_out, not_6_out);
  nand nand_7 (Z2, not_4_out, B1, not_6_out);
  nand nand_8 (Z3, B0, B1, not_6_out);
endmodule

module IC_74147 (
  input  D1,
  input  D2,
  input  D3,
  input  D4,
  input  D5,
  input  D6,
  input  D7,
  input  D8,
  input  D9,
  output Y1,
  output Y2,
  output Y3,
  output Y4
);

  wire and_1_out, and_2_out, and_3_out, and_4_out, and_5_out, and_6_out, and_7_out, and_8_out, and_9_out,
       and_10_out, and_11_out, and_12_out, buffer_1_out, nor_1_out, not_1_out, not_2_out, not_3_out,
       not_4_out, not_5_out, not_6_out, not_7_out, not_8_out, not_9_out, not_10_out, not_11_out, not_12_out,
       not_13_out;

  not not_1 (not_1_out, D1);
  not not_2 (not_2_out, D2);
  not not_3 (not_3_out, D3);
  not not_4 (not_4_out, D4);
  not not_5 (not_5_out, D5);
  not not_6 (not_6_out, D6);
  not not_7 (not_7_out, D7);
  not not_8 (not_8_out, D8);
  not not_9 (not_9_out, D9);
  not not_10 (not_10_out, not_2_out);
  not not_11 (not_11_out, not_4_out);
  not not_12 (not_12_out, not_5_out);
  not not_13 (not_13_out, not_6_out);
  nor nor_1 (nor_1_out, not_8_out, not_9_out);
  and and_1 (and_1_out, not_1_out, not_10_out, not_11_out, not_13_out, nor_1_out);
  and and_2 (and_2_out, not_3_out, not_11_out, not_13_out, nor_1_out);
  and and_3 (and_3_out, not_5_out, not_13_out, nor_1_out);
  and and_4 (and_4_out, not_7_out, nor_1_out);
  buf buffer_1 (buffer_1_out, not_9_out);
  and and_5 (and_5_out, not_2_out, not_11_out, not_12_out, nor_1_out);
  and and_6 (and_6_out, not_3_out, not_11_out, not_12_out, nor_1_out);
  and and_7 (and_7_out, not_6_out, nor_1_out);
  and and_8 (and_8_out, not_7_out, nor_1_out);
  and and_9 (and_9_out, not_4_out, nor_1_out);
  and and_10 (and_10_out, not_5_out, nor_1_out);
  and and_11 (and_11_out, not_6_out, nor_1_out);
  and and_12 (and_12_out, not_7_out, nor_1_out);
  nor nor_2 (Y1, and_1_out, and_2_out, and_3_out, and_4_out, buffer_1_out);
  nor nor_3 (Y2, and_5_out, and_6_out, and_7_out, and_8_out);
  nor nor_4 (Y3, and_9_out, and_10_out, and_11_out, and_12_out);
  nor nor_5 (Y4, not_8_out, not_9_out);
endmodule

module IC_74151 (
  input  A,
  input  B,
  input  C,
  input  D,
  input  E,
  input  F,
  input  G,
  input  J,
  input  S0,
  input  S1,
  input  S2,
  input  OE,
  output Y,
  output Z
);

  wire and_1_out, and_2_out, and_3_out, and_4_out, and_5_out, and_6_out, and_7_out, and_8_out, not_1_out,
       not_2_out, not_3_out, not_4_out;

  not not_1 (not_1_out, S0);
  not not_2 (not_2_out, S1);
  not not_3 (not_3_out, OE);
  not not_4 (not_4_out, S2);
  and and_1 (and_1_out, A, not_3_out, not_1_out, not_2_out, not_4_out);
  and and_2 (and_2_out, B, not_3_out, S0, not_2_out, not_4_out);
  and and_3 (and_3_out, C, not_3_out, not_1_out, S1, not_4_out);
  and and_4 (and_4_out, D, not_3_out, S0, S1, not_4_out);
  and and_5 (and_5_out, E, not_3_out, not_1_out, not_2_out, S2);
  and and_6 (and_6_out, F, not_3_out, S0, not_2_out, S2);
  and and_7 (and_7_out, G, not_3_out, not_1_out, S1, S2);
  and and_8 (and_8_out, J, not_3_out, S0, S1, S2);
  or or_1 (Y, and_1_out, and_2_out, and_3_out, and_4_out, and_5_out, and_6_out, and_7_out, and_8_out);
  not not_5 (Z, Y);
endmodule

module IC_74153 (
  input  A1,
  input  B1,
  input  C1,
  input  D1,
  input  A2,
  input  B2,
  input  C2,
  input  D2,
  input  S0,
  input  S1,
  input  OE1,
  input  OE2,
  output Y1,
  output Y2
);

  wire and_1_out, and_2_out, and_3_out, and_4_out, and_5_out, and_6_out, and_7_out, and_8_out, not_1_out,
       not_2_out, not_3_out, not_4_out;

  not not_1 (not_1_out, S0);
  not not_2 (not_2_out, S1);
  not not_3 (not_3_out, OE1);
  not not_4 (not_4_out, OE2);
  and and_1 (and_1_out, A1, not_3_out, not_1_out, not_2_out);
  and and_2 (and_2_out, B1, not_3_out, S0, not_2_out);
  and and_3 (and_3_out, C1, not_3_out, not_1_out, S1);
  and and_4 (and_4_out, D1, not_3_out, S0, S1);
  and and_5 (and_5_out, A2, not_4_out, not_1_out, not_2_out);
  and and_6 (and_6_out, B2, not_4_out, S0, not_2_out);
  and and_7 (and_7_out, C2, not_4_out, not_1_out, S1);
  and and_8 (and_8_out, D2, not_4_out, S0, S1);
  or or_1 (Y1, and_1_out, and_2_out, and_3_out, and_4_out);
  or or_2 (Y2, and_5_out, and_6_out, and_7_out, and_8_out);
endmodule

module IC_74157 (
  input  A1,
  input  B1,
  input  A2,
  input  B2,
  input  A3,
  input  B3,
  input  A4,
  input  B4,
  input  S0,
  input  OE,
  output Y1,
  output Y2,
  output Y3,
  output Y4
);

  wire and_1_out, and_2_out, and_3_out, and_4_out, and_5_out, and_6_out, and_7_out, and_8_out, not_1_out,
       not_2_out;

  not not_1 (not_1_out, S0);
  not not_2 (not_2_out, OE);
  and and_1 (and_1_out, A1, not_1_out, not_2_out);
  and and_2 (and_2_out, B1, S0, not_2_out);
  and and_3 (and_3_out, A2, not_1_out, not_2_out);
  and and_4 (and_4_out, B2, S0, not_2_out);
  and and_5 (and_5_out, A3, not_1_out, not_2_out);
  and and_6 (and_6_out, B3, S0, not_2_out);
  and and_7 (and_7_out, A4, not_1_out, not_2_out);
  and and_8 (and_8_out, B4, S0, not_2_out);
  or or_1 (Y1, and_1_out, and_2_out);
  or or_2 (Y2, and_3_out, and_4_out);
  or or_3 (Y3, and_5_out, and_6_out);
  or or_4 (Y4, and_7_out, and_8_out);
endmodule

module IC_74161 (
  input  CLK,
  input  CLR,
  input  LE,
  input  CEP,
  input  CET,
  input  D1,
  input  D2,
  input  D3,
  input  D4,
  output Q1,
  output Q2,
  output Q3,
  output Q4,
  output TC
);

  wire and_1_out, and_2_out, and_3_out, and_4_out, and_5_out, and_6_out, and_7_out, and_8_out, and_9_out,
       and_10_out, and_11_out, and_12_out, not_1_out, not_2_out, or_1_out, or_2_out, or_3_out, or_4_out,
       xor_1_out, xor_2_out, xor_3_out, xor_4_out;

  not not_1 (not_1_out, CLR);
  and and_1 (and_1_out, LE, CEP, CET);
  not not_2 (not_2_out, LE);
  and and_2 (and_2_out, D1, not_2_out);
  and and_3 (and_3_out, Q1, LE);
  and and_4 (and_4_out, D2, not_2_out);
  and and_5 (and_5_out, Q2, LE);
  and and_6 (and_6_out, Q1, and_1_out);
  and and_7 (and_7_out, D3, not_2_out);
  and and_8 (and_8_out, Q3, LE);
  and and_9 (and_9_out, Q2, Q1, and_1_out);
  and and_10 (and_10_out, D4, not_2_out);
  and and_11 (and_11_out, Q4, LE);
  and and_12 (and_12_out, Q3, Q2, Q1, and_1_out);
  xor xor_1 (xor_1_out, and_3_out, and_1_out);
  xor xor_2 (xor_2_out, and_5_out, and_6_out);
  xor xor_3 (xor_3_out, and_8_out, and_9_out);
  xor xor_4 (xor_4_out, and_11_out, and_12_out);
  or or_1 (or_1_out, and_2_out, xor_1_out);
  or or_2 (or_2_out, and_4_out, xor_2_out);
  or or_3 (or_3_out, and_7_out, xor_3_out);
  or or_4 (or_4_out, and_10_out, xor_4_out);
  D_Flip_Flop d_flip_flop_1 (.Q(Q1), .CLR(not_1_out), .D(or_1_out), .CLK(CLK));  // open: R, SET
  D_Flip_Flop d_flip_flop_2 (.Q(Q2), .CLR(not_1_out), .D(or_2_out), .CLK(CLK));  // open: R, SET
  D_Flip_Flop d_flip_flop_3 (.Q(Q3), .CLR(not_1_out), .D(or_3_out), .CLK(CLK));  // open: R, SET
  D_Flip_Flop d_flip_flop_4 (.Q(Q4), .CLR(not_1_out), .D(or_4_out), .CLK(CLK));  // open: R, SET
  and and_13 (TC, Q4, Q3, Q2, Q1, CET);
endmodule

module IC_74163 (
  input  CLK,
  input  CE,
  input  LE,
  input  CEP,
  input  CET,
  input  D1,
  input  D2,
  input  D3,
  input  D4,
  output Q1,
  output Q2,
  output Q3,
  output Q4,
  output TC
);

  wire and_1_out, and_2_out, and_3_out, and_4_out, and_5_out, and_6_out, and_7_out, and_8_out, and_9_out,
       and_10_out, and_11_out, and_12_out, and_13_out, not_1_out, not_2_out, not_3_out, or_1_out, or_2_out,
       or_3_out, or_4_out, xor_1_out, xor_2_out, xor_3_out, xor_4_out;

  not not_1 (not_1_out, CLK);
  not not_2 (not_2_out, CE);
  and and_1 (and_1_out, LE, CEP, CET);
  not not_3 (not_3_out, LE);
  and and_2 (and_2_out, D1, not_2_out, not_3_out);
  and and_3 (and_3_out, Q1, not_2_out, LE);
  and and_4 (and_4_out, not_2_out, and_1_out);
  and and_5 (and_5_out, D2, not_2_out, not_3_out);
  and and_6 (and_6_out, Q2, not_2_out, LE);
  and and_7 (and_7_out, Q1, not_2_out, and_1_out);
  and and_8 (and_8_out, D3, not_2_out, not_3_out);
  and and_9 (and_9_out, Q3, not_2_out, LE);
  and and_10 (and_10_out, Q2, Q1, and_1_out, not_2_out);
  and and_11 (and_11_out, D4, not_2_out, not_3_out);
  and and_12 (and_12_out, Q4, not_2_out, LE);
  and and_13 (and_13_out, Q3, Q2, not_2_out, Q1, and_1_out);
  xor xor_1 (xor_1_out, and_3_out, and_4_out);
  xor xor_2 (xor_2_out, and_6_out, and_7_out);
  xor xor_3 (xor_3_out, and_9_out, and_10_out);
  xor xor_4 (xor_4_out, and_12_out, and_13_out);
  or or_1 (or_1_out, and_2_out, xor_1_out);
  or or_2 (or_2_out, and_5_out, xor_2_out);
  or or_3 (or_3_out, and_8_out, xor_3_out);
  or or_4 (or_4_out, and_11_out, xor_4_out);
  D_Flip_Flop d_flip_flop_1 (.Q(Q1), .D(or_1_out), .CLK(not_1_out));  // open: R, SET, CLR
  D_Flip_Flop d_flip_flop_2 (.Q(Q2), .D(or_2_out), .CLK(not_1_out));  // open: R, SET, CLR
  D_Flip_Flop d_flip_flop_3 (.Q(Q3), .D(or_3_out), .CLK(not_1_out));  // open: R, SET, CLR
  D_Flip_Flop d_flip_flop_4 (.Q(Q4), .D(or_4_out), .CLK(not_1_out));  // open: R, SET, CLR
  and and_14 (TC, Q4, Q3, Q2, Q1, CET);
endmodule

module IC_74173 (
  input  D1,
  input  D2,
  input  D3,
  input  D4,
  input  CLK,
  input  CE1,
  input  CE2,
  input  CLR,
  input  OE1,
  input  OE2,
  output Q1,
  output Q2,
  output Q3,
  output Q4
);

  wire and_1_out, d_flip_flop_1_q, d_flip_flop_2_q, d_flip_flop_3_q, d_flip_flop_4_q, nor_1_out, nor_2_out;

  nor nor_1 (nor_1_out, CE1, CE2);
  nor nor_2 (nor_2_out, OE1, OE2);
  and and_1 (and_1_out, CLK, nor_1_out);
  D_Flip_Flop d_flip_flop_1 (.Q(d_flip_flop_1_q), .CLR(CLR), .D(D1), .CLK(and_1_out));  // open: R, SET
  D_Flip_Flop d_flip_flop_2 (.Q(d_flip_flop_2_q), .CLR(CLR), .D(D2), .CLK(and_1_out));  // open: R, SET
  D_Flip_Flop d_flip_flop_3 (.Q(d_flip_flop_3_q), .CLR(CLR), .D(D3), .CLK(and_1_out));  // open: R, SET
  D_Flip_Flop d_flip_flop_4 (.Q(d_flip_flop_4_q), .CLR(CLR), .D(D4), .CLK(and_1_out));  // open: R, SET
  assign Q1 = nor_2_out ? d_flip_flop_1_q : 1'bz;  // Controlled_Buffer controlled_buffer_1
  assign Q2 = nor_2_out ? d_flip_flop_2_q : 1'bz;  // Controlled_Buffer controlled_buffer_2
  assign Q3 = nor_2_out ? d_flip_flop_3_q : 1'bz;  // Controlled_Buffer controlled_buffer_3
  assign Q4 = nor_2_out ? d_flip_flop_4_q : 1'bz;  // Controlled_Buffer controlled_buffer_4
endmodule

module IC_74175 (
  input  D1,
  input  D2,
  input  D3,
  input  D4,
  input  CLK,
  input  CLR,
  output Q1,
  output R1,
  output Q2,
  output R2,
  output Q3,
  output R3,
  output Q4,
  output R4
);

  wire not_1_out;

  not not_1 (not_1_out, CLR);
  D_Flip_Flop d_flip_flop_1 (.Q(Q1), .R(R1), .CLR(not_1_out), .D(D1), .CLK(CLK));  // open: SET
  D_Flip_Flop d_flip_flop_2 (.Q(Q2), .R(R2), .CLR(not_1_out), .D(D2), .CLK(CLK));  // open: SET
  D_Flip_Flop d_flip_flop_3 (.Q(Q3), .R(R3), .CLR(not_1_out), .D(D3), .CLK(CLK));  // open: SET
  D_Flip_Flop d_flip_flop_4 (.Q(Q4), .R(R4), .CLR(not_1_out), .D(D4), .CLK(CLK));  // open: SET
endmodule

module IC_74238 (
  input  A0,
  input  A1,
  input  A2,
  input  OE1,
  input  OE2,
  input  OE3,
  output Y0,
  output Y1,
  output Y2,
  output Y3,
  output Y4,
  output Y5,
  output Y6,
  output Y7
);

  wire and_1_out, not_1_out, not_2_out, not_3_out, not_4_out, not_5_out;

  not not_1 (not_1_out, A0);
  not not_2 (not_2_out, A1);
  not not_3 (not_3_out, A2);
  not not_4 (not_4_out, OE1);
  not not_5 (not_5_out, OE2);
  and and_1 (and_1_out, not_4_out, not_5_out, OE3);
  and and_2 (Y0, not_1_out, not_2_out, not_3_out, and_1_out);
  and and_3 (Y1, A0, not_2_out, not_3_out, and_1_out);
  and and_4 (Y2, not_1_out, A1, not_3_out, and_1_out);
  and and_5 (Y3, A0, A1, not_3_out, and_1_out);
  and and_6 (Y4, not_1_out, not_2_out, A2, and_1_out);
  and and_7 (Y5, A0, not_2_out, A2, and_1_out);
  and and_8 (Y6, not_1_out, A1, A2, and_1_out);
  and and_9 (Y7, A0, A1, A2, and_1_out);
endmodule

module IC_74244 (
  input  A1,
  input  A2,
  input  A3,
  input  A4,
  input  OEA,
  input  B1,
  input  B2,
  input  B3,
  input  B4,
  input  OEB,
  output Y1,
  output Y2,
  output Y3,
  output Y4,
  output Z1,
  output Z2,
  output Z3,
  output Z4
);

  wire not_1_out, not_2_out;

  not not_1 (not_1_out, OEA);
  not not_2 (not_2_out, OEB);
  assign Y1 = not_1_out ? A1 : 1'bz;  // Controlled_Buffer controlled_buffer_1
  assign Y2 = not_1_out ? A2 : 1'bz;  // Controlled_Buffer controlled_buffer_2
  assign Y3 = not_1_out ? A3 : 1'bz;  // Controlled_Buffer controlled_buffer_3
  assign Y4 = not_1_out ? A4 : 1'bz;  // Controlled_Buffer controlled_buffer_4
  assign Z1 = not_2_out ? B1 : 1'bz;  // Controlled_Buffer controlled_buffer_5
  assign Z2 = not_2_out ? B2 : 1'bz;  // Controlled_Buffer controlled_buffer_6
  assign Z3 = not_2_out ? B3 : 1'bz;  // Controlled_Buffer controlled_buffer_7
  assign Z4 = not_2_out ? B4 : 1'bz;  // Controlled_Buffer controlled_buffer_8
endmodule

module IC_74273 (
  input  D1,
  input  D2,
  input  D3,
  input  D4,
  input  D5,
  input  D6,
  input  D7,
  input  D8,
  input  CLK,
  input  CLR,
  output Y1,
  output Y2,
  output Y3,
  output Y4,
  output Y5,
  output Y6,
  output Y7,
  output Y8
);

  wire not_1_out;

  not not_1 (not_1_out, CLR);
  D_Flip_Flop d_flip_flop_1 (.Q(Y1), .CLR(not_1_out), .D(D1), .CLK(CLK));  // open: R, SET
  D_Flip_Flop d_flip_flop_2 (.Q(Y2), .CLR(not_1_out), .D(D2), .CLK(CLK));  // open: R, SET
  D_Flip_Flop d_flip_flop_3 (.Q(Y3), .CLR(not_1_out), .D(D3), .CLK(CLK));  // open: R, SET
  D_Flip_Flop d_flip_flop_4 (.Q(Y4), .CLR(not_1_out), .D(D4), .CLK(CLK));  // open: R, SET
  D_Flip_Flop d_flip_flop_5 (.Q(Y5), .CLR(not_1_out), .D(D5), .CLK(CLK));  // open: R, SET
  D_Flip_Flop d_flip_flop_6 (.Q(Y6), .CLR(not_1_out), .D(D6), .CLK(CLK));  // open: R, SET
  D_Flip_Flop d_flip_flop_7 (.Q(Y7), .CLR(not_1_out), .D(D7), .CLK(CLK));  // open: R, SET
  D_Flip_Flop d_flip_flop_8 (.Q(Y8), .CLR(not_1_out), .D(D8), .CLK(CLK));  // open: R, SET
endmodule

module IC_74283 (
  input  A1,
  input  A2,
  input  A3,
  input  A4,
  input  B1,
  input  B2,
  input  B3,
  input  B4,
  input  CIN,
  output Y1,
  output Y2,
  output Y3,
  output Y4,
  output COUT
);

  wire and_1_out, and_2_out, and_3_out, and_4_out, and_5_out, and_6_out, and_7_out, and_8_out, and_9_out,
       and_10_out, and_11_out, and_12_out, and_13_out, and_14_out, nand_1_out, nand_2_out, nand_3_out,
       nand_4_out, nor_1_out, nor_2_out, nor_3_out, nor_4_out, nor_5_out, nor_6_out, nor_7_out, not_1_out,
       not_2_out, not_3_out, not_4_out, not_5_out, not_6_out;

  not not_1 (not_1_out, CIN);
  nor nor_1 (nor_1_out, A1, B1);
  nand nand_1 (nand_1_out, A1, B1);
  nor nor_2 (nor_2_out, A2, B2);
  nand nand_2 (nand_2_out, A2, B2);
  nor nor_3 (nor_3_out, A3, B3);
  nand nand_3 (nand_3_out, A3, B3);
  nor nor_4 (nor_4_out, A4, B4);
  nand nand_4 (nand_4_out, A4, B4);
  not not_2 (not_2_out, not_1_out);
  not not_3 (not_3_out, nor_1_out);
  and and_1 (and_1_out, not_1_out, nand_1_out);
  not not_4 (not_4_out, nor_2_out);
  and and_2 (and_2_out, not_1_out, nand_1_out, nand_2_out);
  and and_3 (and_3_out, nand_2_out, nor_1_out);
  not not_5 (not_5_out, nor_3_out);
  and and_4 (and_4_out, not_1_out, nand_1_out, nand_2_out, nand_3_out);
  and and_5 (and_5_out, nand_2_out, nand_3_out, nor_1_out);
  and and_6 (and_6_out, nand_3_out, nor_2_out);
  not not_6 (not_6_out, nor_4_out);
  and and_7 (and_7_out, not_1_out, nand_1_out, nand_2_out, nand_3_out, nand_4_out);
  and and_8 (and_8_out, nand_2_out, nand_3_out, nand_4_out, nor_1_out);
  and and_9 (and_9_out, nand_3_out, nand_4_out, nor_2_out);
  and and_10 (and_10_out, nand_4_out, nor_3_out);
  and and_11 (and_11_out, not_3_out, nand_1_out);
  nor nor_5 (nor_5_out, and_1_out, nor_1_out);
  and and_12 (and_12_out, not_4_out, nand_2_out);
  nor nor_6 (nor_6_out, and_2_out, and_3_out, nor_2_out);
  and and_13 (and_13_out, not_5_out, nand_3_out);
  nor nor_7 (nor_7_out, and_4_out, and_5_out, and_6_out, nor_3_out);
  and and_14 (and_14_out, not_6_out, nand_4_out);
  nor nor_8 (COUT, and_7_out, and_8_out, and_9_out, and_10_out, nor_4_out);
  xor xor_1 (Y1, not_2_out, and_11_out);
  xor xor_2 (Y2, nor_5_out, and_12_out);
  xor xor_3 (Y3, nor_6_out, and_13_out);
  xor xor_4 (Y4, nor_7_out, and_14_out);
endmodule

module IC_74374 (
  input  D1,
  input  D2,
  input  D3,
  input  D4,
  input  D5,
  input  D6,
  input  D7,
  input  D8,
  input  CLK,
  input  OE,
  output Y1,
  output Y2,
  output Y3,
  output Y4,
  output Y5,
  output Y6,
  output Y7,
  output Y8
);

  wire d_flip_flop_1_q, d_flip_flop_2_q, d_flip_flop_3_q, d_flip_flop_4_q, d_flip_flop_5_q, d_flip_flop_6_q,
       d_flip_flop_7_q, d_flip_flop_8_q, not_1_out;

  D_Flip_Flop d_flip_flop_1 (.Q(d_flip_flop_1_q), .D(D1), .CLK(CLK));  // open: R, SET, CLR
  D_Flip_Flop d_flip_flop_2 (.Q(d_flip_flop_2_q), .D(D2), .CLK(CLK));  // open: R, SET, CLR
  D_Flip_Flop d_flip_flop_3 (.Q(d_flip_flop_3_q), .D(D3), .CLK(CLK));  // open: R, SET, CLR
  D_Flip_Flop d_flip_flop_4 (.Q(d_flip_flop_4_q), .D(D4), .CLK(CLK));  // open: R, SET, CLR
  D_Flip_Flop d_flip_flop_5 (.Q(d_flip_flop_5_q), .D(D5), .CLK(CLK));  // open: R, SET, CLR
  D_Flip_Flop d_flip_flop_6 (.Q(d_flip_flop_6_q), .D(D6), .CLK(CLK));  // open: R, SET, CLR
  D_Flip_Flop d_flip_flop_7 (.Q(d_flip_flop_7_q), .D(D7), .CLK(CLK));  // open: R, SET, CLR
  D_Flip_Flop d_flip_flop_8 (.Q(d_flip_flop_8_q), .D(D8), .CLK(CLK));  // open: R, SET, CLR
  not not_1 (not_1_out, OE);
  assign Y1 = not_1_out ? d_flip_flop_1_q : 1'bz;  // Controlled_Buffer controlled_buffer_1
  assign Y2 = not_1_out ? d_flip_flop_2_q : 1'bz;  // Controlled_Buffer controlled_buffer_2
  assign Y3 = not_1_out ? d_flip_flop_3_q : 1'bz;  // Controlled_Buffer controlled_buffer_3
  assign Y4 = not_1_out ? d_flip_flop_4_q : 1'bz;  // Controlled_Buffer controlled_buffer_4
  assign Y5 = not_1_out ? d_flip_flop_5_q : 1'bz;  // Controlled_Buffer controlled_buffer_5
  assign Y6 = not_1_out ? d_flip_flop_6_q : 1'bz;  // Controlled_Buffer controlled_buffer_6
  assign Y7 = not_1_out ? d_flip_flop_7_q : 1'bz;  // Controlled_Buffer controlled_buffer_7
  assign Y8 = not_1_out ? d_flip_flop_8_q : 1'bz;  // Controlled_Buffer controlled_buffer_8
endmodule

module IC_74377 (
  input  D1,
  input  D2,
  input  D3,
  input  D4,
  input  D5,
  input  D6,
  input  D7,
  input  D8,
  input  CLK,
  input  CE,
  output Y1,
  output Y2,
  output Y3,
  output Y4,
  output Y5,
  output Y6,
  output Y7,
  output Y8
);

  wire and_1_out, not_1_out;

  not not_1 (not_1_out, CE);
  and and_1 (and_1_out, CLK, not_1_out);
  D_Flip_Flop d_flip_flop_1 (.Q(Y1), .D(D1), .CLK(and_1_out));  // open: R, SET, CLR
  D_Flip_Flop d_flip_flop_2 (.Q(Y2), .D(D2), .CLK(and_1_out));  // open: R, SET, CLR
  D_Flip_Flop d_flip_flop_3 (.Q(Y3), .D(D3), .CLK(and_1_out));  // open: R, SET, CLR
  D_Flip_Flop d_flip_flop_4 (.Q(Y4), .D(D4), .CLK(and_1_out));  // open: R, SET, CLR
  D_Flip_Flop d_flip_flop_5 (.Q(Y5), .D(D5), .CLK(and_1_out));  // open: R, SET, CLR
  D_Flip_Flop d_flip_flop_6 (.Q(Y6), .D(D6), .CLK(and_1_out));  // open: R, SET, CLR
  D_Flip_Flop d_flip_flop_7 (.Q(Y7), .D(D7), .CLK(and_1_out));  // open: R, SET, CLR
  D_Flip_Flop d_flip_flop_8 (.Q(Y8), .D(D8), .CLK(and_1_out));  // open: R, SET, CLR
endmodule

module D_Flip_Flop (
  input  SET,
  input  D,
  input  CLK,
  input  CLR,
  output Q,
  output R
);

  D_Flip_Flop_part d_ff_1 (.D(D), .clk(CLK), .Q(Q), .Qn(R), .preset(SET), .reset(CLR));
endmodule

module D_Latch (
  input  SET,
  input  D,
  input  LE,
  input  CLR,
  output Q,
  output R
);

  D_Flip_Flop_part #(.trigger("high")) d_ff_1 (.D(D), .clk(LE), .Q(Q), .Qn(R), .preset(SET), .reset(CLR));
endmodule

module JK_Flip_Flop (
  input  SET,
  input  J,
  input  CLK,
  input  K,
  input  CLR,
  output Q,
  output R
);

  J_K_Flip_Flop j_k_ff_1 (.J(J), .K(K), .clk(CLK), .Q(Q), .Qn(R), .preset(SET), .reset(CLR));

  // Notes on the sheet:
  //   CLR: pull=down
  //   SET: pull=down
endmodule

module IC_74373 (
  input  D1,
  input  D2,
  input  D3,
  input  D4,
  input  D5,
  input  D6,
  input  D7,
  input  D8,
  input  CLK,
  input  OE,
  output Y1,
  output Y2,
  output Y3,
  output Y4,
  output Y5,
  output Y6,
  output Y7,
  output Y8
);

  wire d_latch_1_q, d_latch_2_q, d_latch_3_q, d_latch_4_q, d_latch_5_q, d_latch_6_q, d_latch_7_q,
       d_latch_8_q, not_1_out;

  D_Latch d_latch_1 (.Q(d_latch_1_q), .D(D1), .LE(CLK));  // open: R, SET, CLR
  D_Latch d_latch_2 (.Q(d_latch_2_q), .D(D2), .LE(CLK));  // open: R, SET, CLR
  D_Latch d_latch_3 (.Q(d_latch_3_q), .D(D3), .LE(CLK));  // open: R, SET, CLR
  D_Latch d_latch_4 (.Q(d_latch_4_q), .D(D4), .LE(CLK));  // open: R, SET, CLR
  D_Latch d_latch_5 (.Q(d_latch_5_q), .D(D5), .LE(CLK));  // open: R, SET, CLR
  D_Latch d_latch_6 (.Q(d_latch_6_q), .D(D6), .LE(CLK));  // open: R, SET, CLR
  D_Latch d_latch_7 (.Q(d_latch_7_q), .D(D7), .LE(CLK));  // open: R, SET, CLR
  D_Latch d_latch_8 (.Q(d_latch_8_q), .D(D8), .LE(CLK));  // open: R, SET, CLR
  not not_1 (not_1_out, OE);
  assign Y1 = not_1_out ? d_latch_1_q : 1'bz;  // Controlled_Buffer controlled_buffer_1
  assign Y2 = not_1_out ? d_latch_2_q : 1'bz;  // Controlled_Buffer controlled_buffer_2
  assign Y3 = not_1_out ? d_latch_3_q : 1'bz;  // Controlled_Buffer controlled_buffer_3
  assign Y4 = not_1_out ? d_latch_4_q : 1'bz;  // Controlled_Buffer controlled_buffer_4
  assign Y5 = not_1_out ? d_latch_5_q : 1'bz;  // Controlled_Buffer controlled_buffer_5
  assign Y6 = not_1_out ? d_latch_6_q : 1'bz;  // Controlled_Buffer controlled_buffer_6
  assign Y7 = not_1_out ? d_latch_7_q : 1'bz;  // Controlled_Buffer controlled_buffer_7
  assign Y8 = not_1_out ? d_latch_8_q : 1'bz;  // Controlled_Buffer controlled_buffer_8
endmodule

module IC_74533 (
  input  D1,
  input  D2,
  input  D3,
  input  D4,
  input  D5,
  input  D6,
  input  D7,
  input  D8,
  input  LE,
  input  OE,
  output Y1,
  output Y2,
  output Y3,
  output Y4,
  output Y5,
  output Y6,
  output Y7,
  output Y8
);

  wire d_latch_1_q, d_latch_2_q, d_latch_3_q, d_latch_4_q, d_latch_5_q, d_latch_6_q, d_latch_7_q,
       d_latch_8_q, not_1_out;

  D_Latch d_latch_1 (.Q(d_latch_1_q), .D(D1), .LE(LE));  // open: R, SET, CLR
  D_Latch d_latch_2 (.Q(d_latch_2_q), .D(D2), .LE(LE));  // open: R, SET, CLR
  D_Latch d_latch_3 (.Q(d_latch_3_q), .D(D3), .LE(LE));  // open: R, SET, CLR
  D_Latch d_latch_4 (.Q(d_latch_4_q), .D(D4), .LE(LE));  // open: R, SET, CLR
  D_Latch d_latch_5 (.Q(d_latch_5_q), .D(D5), .LE(LE));  // open: R, SET, CLR
  D_Latch d_latch_6 (.Q(d_latch_6_q), .D(D6), .LE(LE));  // open: R, SET, CLR
  D_Latch d_latch_7 (.Q(d_latch_7_q), .D(D7), .LE(LE));  // open: R, SET, CLR
  D_Latch d_latch_8 (.Q(d_latch_8_q), .D(D8), .LE(LE));  // open: R, SET, CLR
  not not_1 (not_1_out, OE);
  assign Y1 = not_1_out ? ~d_latch_1_q : 1'bz;  // Controlled_Inverter controlled_inverter_1
  assign Y2 = not_1_out ? ~d_latch_2_q : 1'bz;  // Controlled_Inverter controlled_inverter_2
  assign Y3 = not_1_out ? ~d_latch_3_q : 1'bz;  // Controlled_Inverter controlled_inverter_3
  assign Y4 = not_1_out ? ~d_latch_4_q : 1'bz;  // Controlled_Inverter controlled_inverter_4
  assign Y5 = not_1_out ? ~d_latch_5_q : 1'bz;  // Controlled_Inverter controlled_inverter_5
  assign Y6 = not_1_out ? ~d_latch_6_q : 1'bz;  // Controlled_Inverter controlled_inverter_6
  assign Y7 = not_1_out ? ~d_latch_7_q : 1'bz;  // Controlled_Inverter controlled_inverter_7
  assign Y8 = not_1_out ? ~d_latch_8_q : 1'bz;  // Controlled_Inverter controlled_inverter_8
endmodule

module IC_74240 (
  input  A1,
  input  A2,
  input  A3,
  input  A4,
  input  OEA,
  input  B1,
  input  B2,
  input  B3,
  input  B4,
  input  OEB,
  output Y1,
  output Y2,
  output Y3,
  output Y4,
  output Z1,
  output Z2,
  output Z3,
  output Z4
);

  wire not_1_out, not_2_out;

  not not_1 (not_1_out, OEA);
  not not_2 (not_2_out, OEB);
  assign Y1 = not_1_out ? ~A1 : 1'bz;  // Controlled_Inverter controlled_inverter_1
  assign Y2 = not_1_out ? ~A2 : 1'bz;  // Controlled_Inverter controlled_inverter_2
  assign Y3 = not_1_out ? ~A3 : 1'bz;  // Controlled_Inverter controlled_inverter_3
  assign Y4 = not_1_out ? ~A4 : 1'bz;  // Controlled_Inverter controlled_inverter_4
  assign Z1 = not_2_out ? ~B1 : 1'bz;  // Controlled_Inverter controlled_inverter_5
  assign Z2 = not_2_out ? ~B2 : 1'bz;  // Controlled_Inverter controlled_inverter_6
  assign Z3 = not_2_out ? ~B3 : 1'bz;  // Controlled_Inverter controlled_inverter_7
  assign Z4 = not_2_out ? ~B4 : 1'bz;  // Controlled_Inverter controlled_inverter_8
endmodule
