// Logisim project oisc_D16A16bit_ttl_hc.circ as structural Verilog: 1 circuit, main circuit main
module main (
  input  in_1
);

  wire and_1_out, and_3_out, button_1_out, clock_1_out, ic_7400_1_p3, ic_7400_1_p4, ic_7400_1_p11,
       ic_7400_1_p12, ic_7400_2_p1, ic_7400_2_p2, ic_7400_2_p6, ic_7400_2_p9, ic_7400_2_p10, ic_7400_2_p12,
       ic_7400_3_p2, ic_7400_3_p6, ic_7400_3_p9, ic_7400_3_p11, ic_7400_4_p3, ic_7400_4_p8, ic_7400_4_p10,
       ic_7414_1_p5, ic_7414_1_p6, ic_7414_2_p1, ic_7414_2_p3, ic_7432_1_p1, ic_7432_1_p2, ic_7432_1_p3,
       ic_7432_1_p4, ic_7432_2_p9, ic_7432_2_p10, ic_7432_2_p11, ic_7432_2_p12, ic_7432_3_p9, ic_7432_3_p10,
       ic_7432_3_p11, ic_7432_3_p12, ic_7432_4_p3, ic_7432_4_p7, ic_7476_1_p11, ic_7476_2_p12, ic_7476_2_p13,
       ic_7476_2_p14, ic_74138_1_p1, ic_74138_1_p2, ic_74138_1_p3, ic_74138_1_p4, ic_74138_1_p5,
       ic_74138_1_p6, ic_74138_1_p7, ic_74138_2_p7, ic_74138_2_p8, ic_74138_2_p9, ic_74138_2_p10,
       ic_74138_2_p11, ic_74138_2_p12, ic_74138_2_p13, ic_74161_1_p2, ic_74161_1_p10, ic_74161_2_p1,
       ic_74161_2_p3, ic_74161_2_p6, ic_74161_3_p6, ic_74161_4_p6, ic_74244_1_p1, ic_74244_3_p1,
       ic_74244_5_p10, ic_74273_1_p1, ic_74283_1_p2, ic_74283_2_p2, ic_74283_3_p2, ic_74283_4_p2, not_1_out,
       not_2_out, not_3_out, not_4_out;
  wire [3:0] ic_74161_1_p6, ic_74273_2_p3, ic_74273_3_p11, ic_74273_3_p15, ic_74273_4_p11, ic_74273_4_p15,
       ic_74273_5_p11, ic_74273_5_p15, ic_74273_6_p11, ic_74273_6_p15, undriven, undriven_2, undriven_3,
       undriven_5, undriven_6;
  wire [6:0] keyboard_1_data, ram_1_data_3;
  wire [7:0] ic_7432_2_p1, ram_1_data_2, undriven_4, undriven_7, undriven_8, undriven_9;
  wire [7:7] ram_1_data;

  Clock clock_1 (.out(clock_1_out));
  // Probe on ic_74161_1_p6
  // IC_74161 ic_74161_1: pin names not known; wires that end beside it: clock_1_out, ic_74161_1_p2, 1'b1, 1'b1, 1'b1, ic_74161_1_p6[0], ic_74161_1_p6[1], ic_74161_1_p6[2], ic_74161_1_p6[3], ic_74161_1_p10, ic_74161_1_p6[0], ic_74161_1_p6[1], ic_74161_1_p6[2], ic_74161_1_p6[3], 1'b0, 1'b1
  // IC_74161 ic_74161_2: pin names not known; wires that end beside it: ic_74161_2_p1, ic_74161_1_p2, ic_74161_2_p3, 1'b1, 1'b1, ic_74161_2_p6
  // IC_74161 ic_74161_3: pin names not known; wires that end beside it: ic_74161_2_p1, ic_74161_1_p2, ic_74161_2_p3, 1'b1, ic_74161_2_p6, ic_74161_3_p6
  // IC_74161 ic_74161_4: pin names not known; wires that end beside it: ic_74161_2_p1, ic_74161_1_p2, ic_74161_2_p3, 1'b1, ic_74161_3_p6, ic_74161_4_p6
  // IC_74161 ic_74161_5: pin names not known; wires that end beside it: ic_74161_2_p1, ic_74161_1_p2, ic_74161_2_p3, 1'b1, ic_74161_4_p6
  // Probe on ic_74273_1_p1
  // Probe on ic_74161_1_p10
  // Probe on ic_74244_1_p1
  // Probe on ic_74161_2_p3
  // Probe on ic_74161_2_p1
  // Probe on {undriven_6, undriven_5, undriven_4}
  // Probe on {ic_74273_2_p3, undriven_3, undriven_2, undriven}
  // IC_74273 ic_74273_1: pin names not known; wires that end beside it: ic_74273_1_p1, ic_74161_1_p2
  // IC_74273 ic_74273_2: pin names not known; wires that end beside it: ic_74273_1_p1, ic_74161_1_p2, ic_74273_2_p3[0], ic_74273_2_p3[1], ic_74273_2_p3[2], ic_74273_2_p3[3]
  // IC_74138 ic_74138_1: pin names not known; wires that end beside it: ic_74138_1_p1, ic_74138_1_p2, ic_74138_1_p3, ic_74138_1_p4, ic_74138_1_p5, ic_74138_1_p6, ic_74138_1_p7
  // IC_74138 ic_74138_2: pin names not known; wires that end beside it: ic_74161_1_p6[0], ic_74161_1_p6[1], ic_74161_1_p6[2], 1'b0, 1'b0, ic_74161_1_p6[3], ic_74138_2_p7, ic_74138_2_p8, ic_74138_2_p9, ic_74138_2_p10, ic_74138_2_p11, ic_74138_2_p12, ic_74138_2_p13
  // IC_74244 ic_74244_1: pin names not known; wires that end beside it: ic_74244_1_p1, ic_74244_1_p1
  // IC_74244 ic_74244_2: pin names not known; wires that end beside it: ic_74244_1_p1, ic_74244_1_p1
  // IC_74244 ic_74244_3: pin names not known; wires that end beside it: ic_74244_3_p1, ic_74244_3_p1
  // IC_74244 ic_74244_4: pin names not known; wires that end beside it: ic_74244_3_p1, ic_74244_3_p1
  // IC_7400 ic_7400_1: pin names not known; wires that end beside it: ic_74138_1_p4, ic_74138_2_p7, ic_7400_1_p3, ic_7400_1_p4, ic_74138_1_p5, ic_74138_2_p10, ic_7400_1_p3, ic_7400_1_p4, ic_7400_1_p3, ic_7400_1_p4, ic_7400_1_p11, ic_7400_1_p12
  // IC_7410 ic_7410_1: pin names not known; wires that end beside it: ic_74138_1_p2, ic_74138_1_p3, ic_74138_1_p4, ic_74138_1_p6, ic_74138_1_p7, ic_74138_2_p7, ic_74138_2_p11, ic_74138_2_p12, ic_74138_2_p13, ic_74161_1_p10, ic_74273_1_p1, ic_74161_2_p1
  // Probe on ic_74273_2_p3[3]
  // Probe on {undriven_8, undriven_7}
  Hex_Digit_Display hex_digit_display_1 (.value(ic_74161_1_p6));  // open: dp
  // IC_7400 ic_7400_2: pin names not known; wires that end beside it: ic_7400_2_p1, ic_7400_2_p2, ic_7400_2_p1, undriven_8[7], ic_7400_2_p2, ic_7400_2_p6, ic_7400_2_p1, undriven_8[7], ic_7400_2_p9, ic_7400_2_p10, ic_7400_2_p6, ic_7400_2_p12, ic_7400_2_p12
  // Probe on ic_7400_2_p2
  // IC_7400 ic_7400_3: pin names not known; wires that end beside it: ic_7400_1_p11, ic_7400_3_p2, ic_74138_2_p9, ic_74138_2_p12, ic_7400_1_p12, ic_7400_3_p6, ic_74138_2_p8, ic_74138_2_p13, ic_7400_3_p9, ic_74161_2_p3, ic_7400_3_p11, ic_7400_3_p2
  and and_1 (and_1_out, ic_74138_2_p8, ic_74138_1_p5);
  // Probe on ic_74244_1_p1
  Button button_1 (.out(button_1_out));
  not not_1 (not_1_out, ic_7400_2_p9);
  // Probe on ic_7400_2_p1
  and and_2 (ic_7400_2_p1, ic_7476_2_p14, ic_7400_2_p12);
  // Probe on ic_7476_2_p14
  // Probe on ic_7476_1_p11
  Keyboard #(.buflen(128)) keyboard_1 (.clk(and_3_out), .re(and_3_out), .data(keyboard_1_data));  // open: clr, avail
  Button button_2 ();  // open: out
  RAM #(.addrWidth(16), .dataWidth(16), .databus("bidir"), .trigger("high"), .\type ("nonvolatile")) ram_1 (
    .addr({undriven_8, undriven_7}), .data({ram_1_data_2, ram_1_data[7], ram_1_data_3}));  // open: we, oe, clk
  not not_2 (not_2_out, ic_7400_4_p10);
  // Probe on ic_7400_2_p12
  // IC_7414 ic_7414_1: pin names not known; wires that end beside it: button_1_out, ic_74138_2_p8, ic_74138_1_p5, ic_74161_1_p2, ic_7414_1_p5, ic_7414_1_p6, ic_7414_1_p5, ic_7414_1_p6, ic_7414_1_p5
  // Probe on ic_7414_1_p5
  // Probe on ic_7414_1_p6
  // IC_74244 ic_74244_5: pin names not known; wires that end beside it: ic_7400_2_p2, ram_1_data_3[0], ram_1_data_3[1], ram_1_data_3[2], ram_1_data_3[3], ram_1_data_3[4], ram_1_data_3[5], ram_1_data_3[6], ram_1_data[7], ic_74244_5_p10, keyboard_1_data[0], keyboard_1_data[1], keyboard_1_data[2], keyboard_1_data[3], ic_74244_5_p10, keyboard_1_data[4], keyboard_1_data[5], keyboard_1_data[6], in_1
  not not_3 (not_3_out, ic_74244_5_p10);
  // Probe on ic_7476_2_p12
  // Probe on ic_7400_4_p10
  TTY tty_1 (.data(ram_1_data_3), .clk(ic_7476_2_p12), .we(not_4_out), .clr(button_1_out));
  not not_4 (not_4_out, ic_7400_2_p1);
  // Probe on ic_7476_2_p12
  // IC_7476 ic_7476_1: pin names not known; wires that end beside it: 1'b1, ic_74161_1_p10, clock_1_out, 1'b1, ic_74161_1_p2, 1'b1, ic_7400_3_p9, clock_1_out, ic_7400_3_p9, ic_74161_1_p2, ic_7476_1_p11, ic_74244_1_p1, ic_74244_3_p1
  // IC_7476 ic_7476_2: pin names not known; wires that end beside it: 1'b1, ic_7400_3_p11, clock_1_out, ic_7400_3_p11, ic_74161_1_p2, 1'b1, ic_74273_2_p3[3], and_1_out, 1'b0, ic_74138_1_p1, ic_7400_2_p2, ic_7476_2_p12, ic_7476_2_p13, ic_7476_2_p14
  // IC_7400 ic_7400_4: pin names not known; wires that end beside it: not_2_out, not_1_out, ic_7400_4_p3, ic_7400_2_p12, ic_7476_2_p12, ic_7400_2_p12, ic_7476_2_p12, ic_7400_4_p8, ic_7400_2_p12, ic_7400_4_p10, ic_74244_5_p10, ic_7400_4_p8, ic_74244_5_p10
  // Probe on ic_7400_3_p6
  // Probe on ic_74244_5_p10
  // Probe on ic_7476_2_p13
  and and_3 (and_3_out, not_3_out, ic_7414_1_p5);
  or or_1 (ic_7400_4_p3, ic_7414_1_p6, ic_7414_1_p5);
  // Probe on {ram_1_data_2, ram_1_data[7], ram_1_data_3}
  // IC_7432 ic_7432_1: pin names not known; wires that end beside it: ic_7432_1_p1, ic_7432_1_p2, ic_7432_1_p3, ic_7432_1_p4
  // IC_74273 ic_74273_3: pin names not known; wires that end beside it: ram_1_data_3[0], ram_1_data_3[1], ram_1_data_3[2], ram_1_data_3[3], ram_1_data_3[4], ram_1_data_3[5], ram_1_data_3[6], ram_1_data[7], ic_7414_1_p5, ic_74161_1_p2, ic_74273_3_p11[0], ic_74273_3_p11[1], ic_74273_3_p11[2], ic_74273_3_p11[3], ic_74273_3_p15[0], ic_74273_3_p15[1], ic_74273_3_p15[2], ic_74273_3_p15[3]
  // IC_74273 ic_74273_4: pin names not known; wires that end beside it: ram_1_data_2[0], ram_1_data_2[1], ram_1_data_2[2], ram_1_data_2[3], ram_1_data_2[4], ram_1_data_2[5], ram_1_data_2[6], ram_1_data_2[7], ic_7414_1_p5, ic_74161_1_p2, ic_74273_4_p11[0], ic_74273_4_p11[1], ic_74273_4_p11[2], ic_74273_4_p11[3], ic_74273_4_p15[0], ic_74273_4_p15[1], ic_74273_4_p15[2], ic_74273_4_p15[3]
  // IC_74273 ic_74273_5: pin names not known; wires that end beside it: ram_1_data_3[0], ram_1_data_3[1], ram_1_data_3[2], ram_1_data_3[3], ram_1_data_3[4], ram_1_data_3[5], ram_1_data_3[6], ram_1_data[7], ic_7414_1_p6, ic_74161_1_p2, ic_74273_5_p11[0], ic_74273_5_p11[1], ic_74273_5_p11[2], ic_74273_5_p11[3], ic_74273_5_p15[0], ic_74273_5_p15[1], ic_74273_5_p15[2], ic_74273_5_p15[3]
  // IC_74273 ic_74273_6: pin names not known; wires that end beside it: ram_1_data_2[0], ram_1_data_2[1], ram_1_data_2[2], ram_1_data_2[3], ram_1_data_2[4], ram_1_data_2[5], ram_1_data_2[6], ram_1_data_2[7], ic_7414_1_p6, ic_74161_1_p2, ic_74273_6_p11[0], ic_74273_6_p11[1], ic_74273_6_p11[2], ic_74273_6_p11[3], ic_74273_6_p15[0], ic_74273_6_p15[1], ic_74273_6_p15[2], ic_74273_6_p15[3]
  // Probe on ic_7400_2_p9
  // Probe on ic_7400_2_p10
  // Probe on {ic_74273_4_p15, ic_74273_4_p11, ic_74273_3_p15, ic_74273_3_p11}
  // Probe on {ic_74273_6_p15, ic_74273_6_p11, ic_74273_5_p15, ic_74273_5_p11}
  // DipSwitch dipswitch_1: pin names not known
  // IC_74244 ic_74244_6: pin names not known; wires that end beside it: ic_7400_2_p9, ic_7400_2_p9
  // IC_74244 ic_74244_7: pin names not known; wires that end beside it: ic_7400_2_p9, ic_7400_2_p9
  // IC_74244 ic_74244_8: pin names not known; wires that end beside it: ic_7400_2_p10, ic_7400_2_p10
  // IC_74244 ic_74244_9: pin names not known; wires that end beside it: ic_7400_2_p10, ic_7400_2_p10
  // IC_7432 ic_7432_2: pin names not known; wires that end beside it: ic_7432_2_p1[0], ic_7432_2_p1[1], ic_7432_2_p1[2], ic_7432_2_p1[3], ic_7432_2_p1[4], ic_7432_2_p1[5], ic_7432_2_p1[6], ic_7432_2_p1[7], ic_7432_2_p9, ic_7432_2_p10, ic_7432_2_p11, ic_7432_2_p12
  // IC_7432 ic_7432_3: pin names not known; wires that end beside it: ic_7432_2_p9, ic_7432_2_p10, ic_7432_2_p11, ic_7432_2_p12, ic_7432_1_p1, ic_7432_1_p2, ic_7432_1_p3, ic_7432_1_p4, ic_7432_3_p9, ic_7432_3_p10, ic_7432_3_p11, ic_7432_3_p12
  // IC_74240 ic_74240_1: pin names not known; wires that end beside it: ic_74273_5_p11[0], ic_74273_5_p11[1], ic_74273_5_p11[2], ic_74273_5_p11[3], 1'b0, ic_74273_5_p15[0], ic_74273_5_p15[1], ic_74273_5_p15[2], ic_74273_5_p15[3], 1'b0
  // IC_74240 ic_74240_2: pin names not known; wires that end beside it: ic_74273_6_p11[0], ic_74273_6_p11[1], ic_74273_6_p11[2], ic_74273_6_p11[3], 1'b0, ic_74273_6_p15[0], ic_74273_6_p15[1], ic_74273_6_p15[2], ic_74273_6_p15[3], 1'b0
  // IC_7414 ic_7414_2: pin names not known; wires that end beside it: ic_7414_2_p1, ic_7400_3_p6, ic_7414_2_p3
  // IC_7432 ic_7432_4: pin names not known; wires that end beside it: ic_7432_3_p9, ic_7432_3_p10, ic_7432_4_p3, ic_7432_2_p1[7], ic_7432_3_p11, ic_7432_3_p12, ic_7432_4_p7, ic_7414_2_p3, ic_7432_4_p3, ic_7432_4_p7, ic_7414_2_p1, ic_7400_3_p6
  // IC_74283 ic_74283_1: pin names not known; wires that end beside it: 1'b1, ic_74283_1_p2
  // IC_74283 ic_74283_2: pin names not known; wires that end beside it: ic_74283_1_p2, ic_74283_2_p2
  // IC_74283 ic_74283_3: pin names not known; wires that end beside it: ic_74283_2_p2, ic_74283_3_p2
  // IC_74283 ic_74283_4: pin names not known; wires that end beside it: ic_74283_3_p2, ic_74283_4_p2
  // Probe on ic_74283_4_p2
  // Probe on {ic_7432_2_p1, undriven_9}

  // Notes on the sheet:
  //   DaHai's OISC SUBLEQ
  //   test: hw_d8_.txt
endmodule
