// Logisim project oisc_D16A16bit_ttl_style.circ as structural Verilog: 1 circuit, main circuit main
module main (
);

  wire button_1_out, clock_1_out, ic_7400_1_y1, ic_7400_1_y2, ic_7400_1_y3, ic_7400_1_y4, ic_7400_2_y1,
       ic_7400_2_y2, ic_7400_2_y3, ic_7400_2_y4, ic_7400_3_y1, ic_7400_3_y2, ic_7400_3_y3, ic_7400_3_y4,
       ic_7410_1_y1, ic_7410_1_y2, ic_7410_1_y3, ic_7414_1_y1, ic_7414_1_y5, ic_7414_1_y6, ic_7414_2_y1,
       ic_7432_1_y1, ic_7432_1_y2, ic_7432_1_y3, ic_7432_1_y4, ic_7432_2_y1, ic_7432_2_y2, ic_7432_2_y3,
       ic_7432_2_y4, ic_7432_3_y1, ic_7432_3_y2, ic_7432_3_y3, ic_7432_3_y4, ic_7432_4_y1, ic_7432_4_y2,
       ic_7432_4_y3, ic_7432_4_y4, ic_7476_1_q1, ic_7476_1_q2, ic_7476_1_r2, ic_7476_2_q1, ic_7476_2_r1,
       ic_74138_1_y2, ic_74138_1_y3, ic_74138_1_y4, ic_74138_1_y5, ic_74138_1_y6, ic_74138_1_y7,
       ic_74138_2_y0, ic_74138_2_y1, ic_74138_2_y2, ic_74138_2_y3, ic_74138_2_y4, ic_74138_2_y5,
       ic_74138_2_y6, ic_74161_2_tc, ic_74161_3_tc, ic_74161_4_tc, ic_74283_1_cout, ic_74283_2_cout,
       ic_74283_3_cout, ic_74283_4_cout, not_1_out;
  wire [3:0] ic_74161_1_q1, ic_74161_4_q1, ic_74161_5_q1, ic_74240_1_y1, ic_74240_1_z1, ic_74240_2_y1,
       ic_74240_2_z1, ic_74273_1_y1, ic_74273_1_y5, ic_74273_2_y1, ic_74273_2_y5, ic_74273_3_y1,
       ic_74273_3_y5, ic_74273_4_y1, ic_74273_4_y5, ic_74273_5_y1, ic_74273_5_y5, ic_74273_6_y1,
       ic_74273_6_y5;
  wire [6:0] ram_1_data_3;
  wire [7:0] ic_74161_2_q1, ic_74244_1_y1, ic_74244_2_y1, ic_74283_1_y1, ic_74283_3_y1, ram_1_data_2;
  wire [7:7] ram_1_data;

  Clock clock_1 (.out(clock_1_out));
  // Probe on ic_74161_1_q1
  IC_74161 ic_74161_1 (
    .CLK(clock_1_out), .CLR(ic_7414_1_y1), .LE(1'b1), .CEP(1'b1), .CET(1'b1), .Q1(ic_74161_1_q1[0]),
    .Q2(ic_74161_1_q1[1]), .Q3(ic_74161_1_q1[2]), .Q4(ic_74161_1_q1[3]));  // open: D1, D2, D3, D4, TC
  IC_74161 ic_74161_2 (
    .CLK(ic_7410_1_y3), .CLR(ic_7414_1_y1), .LE(ic_7400_2_y2), .CEP(1'b1), .CET(1'b1), .D1(ic_74273_1_y1[0]),
    .D2(ic_74273_1_y1[1]), .D3(ic_74273_1_y1[2]), .D4(ic_74273_1_y1[3]), .Q1(ic_74161_2_q1[0]),
    .Q2(ic_74161_2_q1[1]), .Q3(ic_74161_2_q1[2]), .Q4(ic_74161_2_q1[3]), .TC(ic_74161_2_tc));
  IC_74161 ic_74161_3 (
    .CLK(ic_7410_1_y3), .CLR(ic_7414_1_y1), .LE(ic_7400_2_y2), .CEP(1'b1), .CET(ic_74161_2_tc),
    .D1(ic_74273_1_y5[0]), .D2(ic_74273_1_y5[1]), .D3(ic_74273_1_y5[2]), .D4(ic_74273_1_y5[3]),
    .Q1(ic_74161_2_q1[4]), .Q2(ic_74161_2_q1[5]), .Q3(ic_74161_2_q1[6]), .Q4(ic_74161_2_q1[7]),
    .TC(ic_74161_3_tc));
  IC_74161 ic_74161_4 (
    .CLK(ic_7410_1_y3), .CLR(ic_7414_1_y1), .LE(ic_7400_2_y2), .CEP(1'b1), .CET(ic_74161_3_tc),
    .D1(ic_74273_2_y1[0]), .D2(ic_74273_2_y1[1]), .D3(ic_74273_2_y1[2]), .D4(ic_74273_2_y1[3]),
    .Q1(ic_74161_4_q1[0]), .Q2(ic_74161_4_q1[1]), .Q3(ic_74161_4_q1[2]), .Q4(ic_74161_4_q1[3]),
    .TC(ic_74161_4_tc));
  IC_74161 ic_74161_5 (
    .CLK(ic_7410_1_y3), .CLR(ic_7414_1_y1), .LE(ic_7400_2_y2), .CEP(1'b1), .CET(ic_74161_4_tc),
    .D1(ic_74273_2_y5[0]), .D2(ic_74273_2_y5[1]), .D3(ic_74273_2_y5[2]), .D4(ic_74273_2_y5[3]),
    .Q1(ic_74161_5_q1[0]), .Q2(ic_74161_5_q1[1]), .Q3(ic_74161_5_q1[2]), .Q4(ic_74161_5_q1[3]));  // open: TC
  // Probe on ic_7410_1_y2
  // Probe on ic_7410_1_y1
  // Probe on ic_7476_1_q2
  // Probe on ic_7400_2_y2
  // Probe on ic_7410_1_y3
  // Probe on {ic_74161_5_q1, ic_74161_4_q1, ic_74161_2_q1}
  // Probe on {ic_74273_2_y5, ic_74273_2_y1, ic_74273_1_y5, ic_74273_1_y1}
  IC_74273 ic_74273_1 (
    .D1(ram_1_data_3[0]), .D2(ram_1_data_3[1]), .D3(ram_1_data_3[2]), .D4(ram_1_data_3[3]),
    .D5(ram_1_data_3[4]), .D6(ram_1_data_3[5]), .D7(ram_1_data_3[6]), .D8(ram_1_data[7]), .CLK(ic_7410_1_y2),
    .CLR(ic_7414_1_y1), .Y1(ic_74273_1_y1[0]), .Y2(ic_74273_1_y1[1]), .Y3(ic_74273_1_y1[2]),
    .Y4(ic_74273_1_y1[3]), .Y5(ic_74273_1_y5[0]), .Y6(ic_74273_1_y5[1]), .Y7(ic_74273_1_y5[2]),
    .Y8(ic_74273_1_y5[3]));
  IC_74273 ic_74273_2 (
    .D1(ram_1_data_2[0]), .D2(ram_1_data_2[1]), .D3(ram_1_data_2[2]), .D4(ram_1_data_2[3]),
    .D5(ram_1_data_2[4]), .D6(ram_1_data_2[5]), .D7(ram_1_data_2[6]), .D8(ram_1_data_2[7]),
    .CLK(ic_7410_1_y2), .CLR(ic_7414_1_y1), .Y1(ic_74273_2_y1[0]), .Y2(ic_74273_2_y1[1]),
    .Y3(ic_74273_2_y1[2]), .Y4(ic_74273_2_y1[3]), .Y5(ic_74273_2_y5[0]), .Y6(ic_74273_2_y5[1]),
    .Y7(ic_74273_2_y5[2]), .Y8(ic_74273_2_y5[3]));
  IC_74138 ic_74138_1 (
    .A0(ic_74161_1_q1[0]), .A1(ic_74161_1_q1[1]), .A2(ic_74161_1_q1[2]), .OE1(ic_74161_1_q1[3]), .OE2(1'b0),
    .OE3(1'b1), .Y2(ic_74138_1_y2), .Y3(ic_74138_1_y3), .Y4(ic_74138_1_y4), .Y5(ic_74138_1_y5),
    .Y6(ic_74138_1_y6), .Y7(ic_74138_1_y7));  // open: Y0, Y1
  IC_74138 ic_74138_2 (
    .A0(ic_74161_1_q1[0]), .A1(ic_74161_1_q1[1]), .A2(ic_74161_1_q1[2]), .OE1(1'b0), .OE2(1'b0),
    .OE3(ic_74161_1_q1[3]), .Y0(ic_74138_2_y0), .Y1(ic_74138_2_y1), .Y2(ic_74138_2_y2), .Y3(ic_74138_2_y3),
    .Y4(ic_74138_2_y4), .Y5(ic_74138_2_y5), .Y6(ic_74138_2_y6));  // open: Y7
  IC_74244 ic_74244_1 (
    .A1(ic_74161_2_q1[0]), .A2(ic_74161_2_q1[1]), .A3(ic_74161_2_q1[2]), .A4(ic_74161_2_q1[3]),
    .OEA(ic_7476_1_q2), .B1(ic_74161_2_q1[4]), .B2(ic_74161_2_q1[5]), .B3(ic_74161_2_q1[6]),
    .B4(ic_74161_2_q1[7]), .OEB(ic_7476_1_q2), .Y1(ic_74244_1_y1[0]), .Y2(ic_74244_1_y1[1]),
    .Y3(ic_74244_1_y1[2]), .Y4(ic_74244_1_y1[3]), .Z1(ic_74244_1_y1[4]), .Z2(ic_74244_1_y1[5]),
    .Z3(ic_74244_1_y1[6]), .Z4(ic_74244_1_y1[7]));
  IC_74244 ic_74244_2 (
    .A1(ic_74161_4_q1[0]), .A2(ic_74161_4_q1[1]), .A3(ic_74161_4_q1[2]), .A4(ic_74161_4_q1[3]),
    .OEA(ic_7476_1_q2), .B1(ic_74161_5_q1[0]), .B2(ic_74161_5_q1[1]), .B3(ic_74161_5_q1[2]),
    .B4(ic_74161_5_q1[3]), .OEB(ic_7476_1_q2), .Y1(ic_74244_2_y1[0]), .Y2(ic_74244_2_y1[1]),
    .Y3(ic_74244_2_y1[2]), .Y4(ic_74244_2_y1[3]), .Z1(ic_74244_2_y1[4]), .Z2(ic_74244_2_y1[5]),
    .Z3(ic_74244_2_y1[6]), .Z4(ic_74244_2_y1[7]));
  IC_74244 ic_74244_3 (
    .A1(ic_74273_1_y1[0]), .A2(ic_74273_1_y1[1]), .A3(ic_74273_1_y1[2]), .A4(ic_74273_1_y1[3]),
    .OEA(ic_7476_1_r2), .B1(ic_74273_1_y5[0]), .B2(ic_74273_1_y5[1]), .B3(ic_74273_1_y5[2]),
    .B4(ic_74273_1_y5[3]), .OEB(ic_7476_1_r2), .Y1(ic_74244_1_y1[0]), .Y2(ic_74244_1_y1[1]),
    .Y3(ic_74244_1_y1[2]), .Y4(ic_74244_1_y1[3]), .Z1(ic_74244_1_y1[4]), .Z2(ic_74244_1_y1[5]),
    .Z3(ic_74244_1_y1[6]), .Z4(ic_74244_1_y1[7]));
  IC_74244 ic_74244_4 (
    .A1(ic_74273_2_y1[0]), .A2(ic_74273_2_y1[1]), .A3(ic_74273_2_y1[2]), .A4(ic_74273_2_y1[3]),
    .OEA(ic_7476_1_r2), .B1(ic_74273_2_y5[0]), .B2(ic_74273_2_y5[1]), .B3(ic_74273_2_y5[2]),
    .B4(ic_74273_2_y5[3]), .OEB(ic_7476_1_r2), .Y1(ic_74244_2_y1[0]), .Y2(ic_74244_2_y1[1]),
    .Y3(ic_74244_2_y1[2]), .Y4(ic_74244_2_y1[3]), .Z1(ic_74244_2_y1[4]), .Z2(ic_74244_2_y1[5]),
    .Z3(ic_74244_2_y1[6]), .Z4(ic_74244_2_y1[7]));
  IC_7400 ic_7400_1 (
    .A1(ic_74138_1_y4), .A2(ic_74138_2_y0), .A3(ic_7400_1_y1), .A4(ic_7400_1_y2), .B1(ic_74138_1_y5),
    .B2(ic_74138_2_y3), .B3(ic_7400_1_y1), .B4(ic_7400_1_y2), .Y1(ic_7400_1_y1), .Y2(ic_7400_1_y2),
    .Y3(ic_7400_1_y3), .Y4(ic_7400_1_y4));
  IC_7410 ic_7410_1 (
    .A1(ic_74138_1_y2), .A2(ic_74138_1_y3), .A3(ic_74138_1_y4), .B1(ic_74138_1_y6), .B2(ic_74138_1_y7),
    .B3(ic_74138_2_y0), .C1(ic_74138_2_y4), .C2(ic_74138_2_y5), .C3(ic_74138_2_y6), .Y1(ic_7410_1_y1),
    .Y2(ic_7410_1_y2), .Y3(ic_7410_1_y3));
  Button button_1 (.out(button_1_out));
  Hex_Digit_Display hex_digit_display_1 (.value(ic_74161_1_q1));  // open: dp
  IC_7400 ic_7400_2 (
    .A1(ic_7400_1_y3), .A2(ic_7400_2_y4), .A3(ic_74138_2_y2), .A4(ic_74138_2_y5), .B1(ic_7400_1_y4),
    .B2(ic_7432_4_y4), .B3(ic_74138_2_y1), .B4(ic_74138_2_y6), .Y1(ic_7400_2_y1), .Y2(ic_7400_2_y2),
    .Y3(ic_7400_2_y3), .Y4(ic_7400_2_y4));
  // Probe on ic_7476_1_q2
  // Probe on {ic_74244_2_y1, ic_74244_1_y1}
  IC_7400 ic_7400_3 (
    .A1(ic_7400_3_y4), .A2(ic_7476_2_q1), .A3(ic_7400_3_y4), .A4(ic_74244_2_y1[6]), .B1(ic_7476_2_q1),
    .B2(ic_7400_3_y3), .B3(ic_7400_3_y4), .B4(ic_74244_2_y1[7]), .Y1(ic_7400_3_y1), .Y2(ic_7400_3_y2),
    .Y3(ic_7400_3_y3), .Y4(ic_7400_3_y4));
  // Probe on ic_7476_1_q1
  RAM #(.addrWidth(16), .dataWidth(16), .databus("bidir"), .trigger("high")) ram_1 (
    .addr({ic_74244_2_y1, ic_74244_1_y1}), .we(ic_7476_2_q1), .oe(ic_7476_2_r1),
    .data({ram_1_data_2, ram_1_data[7], ram_1_data_3}));
  // Probe on ic_7400_3_y4
  // Probe on ic_7476_2_q1
  IC_7414 ic_7414_1 (
    .A1(button_1_out), .A5(ic_74138_2_y1), .A6(ic_74138_1_y5), .Y1(ic_7414_1_y1), .Y5(ic_7414_1_y5),
    .Y6(ic_7414_1_y6));  // open: A2, A3, A4, Y2, Y3, Y4
  // Probe on ic_7414_1_y5
  // Probe on ic_7414_1_y6
  TTY tty_1 (.data(ram_1_data_3), .clk(ic_7476_2_r1), .we(not_1_out), .clr(button_1_out));
  not not_1 (not_1_out, ic_7400_3_y4);
  // Probe on ic_7476_2_r1
  IC_7476 ic_7476_1 (
    .SET1(1'b1), .J1(ic_7410_1_y1), .CLK1(clock_1_out), .K1(1'b1), .CLR1(ic_7414_1_y1), .SET2(1'b1),
    .J2(ic_7400_2_y1), .CLK2(clock_1_out), .K2(ic_7400_2_y1), .CLR2(ic_7414_1_y1), .Q1(ic_7476_1_q1),
    .Q2(ic_7476_1_q2), .R2(ic_7476_1_r2));  // open: R1
  IC_7476 ic_7476_2 (
    .SET1(1'b1), .J1(ic_7400_2_y3), .CLK1(clock_1_out), .K1(ic_7400_2_y3), .CLR1(ic_7414_1_y1), .SET2(1'b1),
    .CLK2(clock_1_out), .CLR2(ic_7414_1_y1), .Q1(ic_7476_2_q1), .R1(ic_7476_2_r1));  // open: J2, K2, Q2, R2
  // Probe on ic_7432_4_y4
  // Probe on ic_7476_2_r1
  // Probe on ic_7400_3_y1
  // Probe on ic_7400_3_y2
  // Probe on {ram_1_data_2, ram_1_data[7], ram_1_data_3}
  IC_74273 ic_74273_3 (
    .D1(ram_1_data_3[0]), .D2(ram_1_data_3[1]), .D3(ram_1_data_3[2]), .D4(ram_1_data_3[3]),
    .D5(ram_1_data_3[4]), .D6(ram_1_data_3[5]), .D7(ram_1_data_3[6]), .D8(ram_1_data[7]), .CLK(ic_7414_1_y5),
    .CLR(ic_7414_1_y1), .Y1(ic_74273_3_y1[0]), .Y2(ic_74273_3_y1[1]), .Y3(ic_74273_3_y1[2]),
    .Y4(ic_74273_3_y1[3]), .Y5(ic_74273_3_y5[0]), .Y6(ic_74273_3_y5[1]), .Y7(ic_74273_3_y5[2]),
    .Y8(ic_74273_3_y5[3]));
  IC_74273 ic_74273_4 (
    .D1(ram_1_data_2[0]), .D2(ram_1_data_2[1]), .D3(ram_1_data_2[2]), .D4(ram_1_data_2[3]),
    .D5(ram_1_data_2[4]), .D6(ram_1_data_2[5]), .D7(ram_1_data_2[6]), .D8(ram_1_data_2[7]),
    .CLK(ic_7414_1_y5), .CLR(ic_7414_1_y1), .Y1(ic_74273_4_y1[0]), .Y2(ic_74273_4_y1[1]),
    .Y3(ic_74273_4_y1[2]), .Y4(ic_74273_4_y1[3]), .Y5(ic_74273_4_y5[0]), .Y6(ic_74273_4_y5[1]),
    .Y7(ic_74273_4_y5[2]), .Y8(ic_74273_4_y5[3]));
  IC_74273 ic_74273_5 (
    .D1(ram_1_data_3[0]), .D2(ram_1_data_3[1]), .D3(ram_1_data_3[2]), .D4(ram_1_data_3[3]),
    .D5(ram_1_data_3[4]), .D6(ram_1_data_3[5]), .D7(ram_1_data_3[6]), .D8(ram_1_data[7]), .CLK(ic_7414_1_y6),
    .CLR(ic_7414_1_y1), .Y1(ic_74273_5_y1[0]), .Y2(ic_74273_5_y1[1]), .Y3(ic_74273_5_y1[2]),
    .Y4(ic_74273_5_y1[3]), .Y5(ic_74273_5_y5[0]), .Y6(ic_74273_5_y5[1]), .Y7(ic_74273_5_y5[2]),
    .Y8(ic_74273_5_y5[3]));
  IC_74273 ic_74273_6 (
    .D1(ram_1_data_2[0]), .D2(ram_1_data_2[1]), .D3(ram_1_data_2[2]), .D4(ram_1_data_2[3]),
    .D5(ram_1_data_2[4]), .D6(ram_1_data_2[5]), .D7(ram_1_data_2[6]), .D8(ram_1_data_2[7]),
    .CLK(ic_7414_1_y6), .CLR(ic_7414_1_y1), .Y1(ic_74273_6_y1[0]), .Y2(ic_74273_6_y1[1]),
    .Y3(ic_74273_6_y1[2]), .Y4(ic_74273_6_y1[3]), .Y5(ic_74273_6_y5[0]), .Y6(ic_74273_6_y5[1]),
    .Y7(ic_74273_6_y5[2]), .Y8(ic_74273_6_y5[3]));
  IC_7432 ic_7432_1 (
    .A1(ic_74283_1_y1[0]), .A2(ic_74283_1_y1[1]), .A3(ic_74283_1_y1[2]), .A4(ic_74283_1_y1[3]),
    .B1(ic_74283_1_y1[4]), .B2(ic_74283_1_y1[5]), .B3(ic_74283_1_y1[6]), .B4(ic_74283_1_y1[7]),
    .Y1(ic_7432_1_y1), .Y2(ic_7432_1_y2), .Y3(ic_7432_1_y3), .Y4(ic_7432_1_y4));
  // Probe on {ic_74273_4_y5, ic_74273_4_y1, ic_74273_3_y5, ic_74273_3_y1}
  // Probe on {ic_74273_6_y5, ic_74273_6_y1, ic_74273_5_y5, ic_74273_5_y1}
  IC_74244 ic_74244_5 (
    .A1(ic_74283_1_y1[7]), .A2(ic_74283_1_y1[6]), .A3(ic_74283_1_y1[5]), .A4(ic_74283_1_y1[4]),
    .OEA(ic_7400_3_y1), .B1(ic_74283_1_y1[3]), .B2(ic_74283_1_y1[2]), .B3(ic_74283_1_y1[1]),
    .B4(ic_74283_1_y1[0]), .OEB(ic_7400_3_y1), .Y1(ram_1_data[7]), .Y2(ram_1_data_3[6]),
    .Y3(ram_1_data_3[5]), .Y4(ram_1_data_3[4]), .Z1(ram_1_data_3[3]), .Z2(ram_1_data_3[2]),
    .Z3(ram_1_data_3[1]), .Z4(ram_1_data_3[0]));
  IC_74244 ic_74244_6 (
    .A1(ic_74283_3_y1[7]), .A2(ic_74283_3_y1[6]), .A3(ic_74283_3_y1[5]), .A4(ic_74283_3_y1[4]),
    .OEA(ic_7400_3_y1), .B1(ic_74283_3_y1[3]), .B2(ic_74283_3_y1[2]), .B3(ic_74283_3_y1[1]),
    .B4(ic_74283_3_y1[0]), .OEB(ic_7400_3_y1), .Y1(ram_1_data_2[7]), .Y2(ram_1_data_2[6]),
    .Y3(ram_1_data_2[5]), .Y4(ram_1_data_2[4]), .Z1(ram_1_data_2[3]), .Z2(ram_1_data_2[2]),
    .Z3(ram_1_data_2[1]), .Z4(ram_1_data_2[0]));
  IC_74244 ic_74244_7 (
    .A1(ic_74273_5_y5[3]), .A2(ic_74273_5_y5[2]), .A3(ic_74273_5_y5[1]), .A4(ic_74273_5_y5[0]),
    .OEA(ic_7400_3_y2), .B1(ic_74273_5_y1[3]), .B2(ic_74273_5_y1[2]), .B3(ic_74273_5_y1[1]),
    .B4(ic_74273_5_y1[0]), .OEB(ic_7400_3_y2), .Y1(ram_1_data[7]), .Y2(ram_1_data_3[6]),
    .Y3(ram_1_data_3[5]), .Y4(ram_1_data_3[4]), .Z1(ram_1_data_3[3]), .Z2(ram_1_data_3[2]),
    .Z3(ram_1_data_3[1]), .Z4(ram_1_data_3[0]));
  IC_74244 ic_74244_8 (
    .A1(ic_74273_6_y5[3]), .A2(ic_74273_6_y5[2]), .A3(ic_74273_6_y5[1]), .A4(ic_74273_6_y5[0]),
    .OEA(ic_7400_3_y2), .B1(ic_74273_6_y1[3]), .B2(ic_74273_6_y1[2]), .B3(ic_74273_6_y1[1]),
    .B4(ic_74273_6_y1[0]), .OEB(ic_7400_3_y2), .Y1(ram_1_data_2[7]), .Y2(ram_1_data_2[6]),
    .Y3(ram_1_data_2[5]), .Y4(ram_1_data_2[4]), .Z1(ram_1_data_2[3]), .Z2(ram_1_data_2[2]),
    .Z3(ram_1_data_2[1]), .Z4(ram_1_data_2[0]));
  IC_7432 ic_7432_2 (
    .A1(ic_74283_3_y1[0]), .A2(ic_74283_3_y1[1]), .A3(ic_74283_3_y1[2]), .A4(ic_74283_3_y1[3]),
    .B1(ic_74283_3_y1[4]), .B2(ic_74283_3_y1[5]), .B3(ic_74283_3_y1[6]), .B4(ic_74283_3_y1[7]),
    .Y1(ic_7432_2_y1), .Y2(ic_7432_2_y2), .Y3(ic_7432_2_y3), .Y4(ic_7432_2_y4));
  IC_74240 ic_74240_1 (
    .A1(ic_74273_5_y1[0]), .A2(ic_74273_5_y1[1]), .A3(ic_74273_5_y1[2]), .A4(ic_74273_5_y1[3]), .OEA(1'b0),
    .B1(ic_74273_5_y5[0]), .B2(ic_74273_5_y5[1]), .B3(ic_74273_5_y5[2]), .B4(ic_74273_5_y5[3]), .OEB(1'b0),
    .Y1(ic_74240_1_y1[0]), .Y2(ic_74240_1_y1[1]), .Y3(ic_74240_1_y1[2]), .Y4(ic_74240_1_y1[3]),
    .Z1(ic_74240_1_z1[0]), .Z2(ic_74240_1_z1[1]), .Z3(ic_74240_1_z1[2]), .Z4(ic_74240_1_z1[3]));
  IC_74240 ic_74240_2 (
    .A1(ic_74273_6_y1[0]), .A2(ic_74273_6_y1[1]), .A3(ic_74273_6_y1[2]), .A4(ic_74273_6_y1[3]), .OEA(1'b0),
    .B1(ic_74273_6_y5[0]), .B2(ic_74273_6_y5[1]), .B3(ic_74273_6_y5[2]), .B4(ic_74273_6_y5[3]), .OEB(1'b0),
    .Y1(ic_74240_2_y1[0]), .Y2(ic_74240_2_y1[1]), .Y3(ic_74240_2_y1[2]), .Y4(ic_74240_2_y1[3]),
    .Z1(ic_74240_2_z1[0]), .Z2(ic_74240_2_z1[1]), .Z3(ic_74240_2_z1[2]), .Z4(ic_74240_2_z1[3]));
  IC_7414 ic_7414_2 (
    .A1(ic_7432_4_y3), .A2(ic_7432_4_y4), .Y1(ic_7414_2_y1));  // open: A3, A4, A5, A6, Y2, Y3, Y4, Y5, Y6
  IC_7432 ic_7432_3 (
    .A1(ic_7432_2_y1), .A2(ic_7432_2_y2), .A3(ic_7432_2_y3), .A4(ic_7432_2_y4), .B1(ic_7432_1_y1),
    .B2(ic_7432_1_y2), .B3(ic_7432_1_y3), .B4(ic_7432_1_y4), .Y1(ic_7432_3_y1), .Y2(ic_7432_3_y2),
    .Y3(ic_7432_3_y3), .Y4(ic_7432_3_y4));
  IC_7432 ic_7432_4 (
    .A1(ic_7432_3_y1), .A2(ic_7432_3_y2), .A3(ic_7432_4_y1), .A4(ic_74283_3_y1[7]), .B1(ic_7432_3_y3),
    .B2(ic_7432_3_y4), .B3(ic_7432_4_y2), .B4(ic_7414_2_y1), .Y1(ic_7432_4_y1), .Y2(ic_7432_4_y2),
    .Y3(ic_7432_4_y3), .Y4(ic_7432_4_y4));
  IC_74283 ic_74283_1 (
    .A1(ic_74273_3_y1[0]), .A2(ic_74273_3_y1[1]), .A3(ic_74273_3_y1[2]), .A4(ic_74273_3_y1[3]),
    .B1(ic_74240_1_y1[0]), .B2(ic_74240_1_y1[1]), .B3(ic_74240_1_y1[2]), .B4(ic_74240_1_y1[3]), .CIN(1'b1),
    .Y1(ic_74283_1_y1[0]), .Y2(ic_74283_1_y1[1]), .Y3(ic_74283_1_y1[2]), .Y4(ic_74283_1_y1[3]),
    .COUT(ic_74283_1_cout));
  IC_74283 ic_74283_2 (
    .A1(ic_74273_3_y5[0]), .A2(ic_74273_3_y5[1]), .A3(ic_74273_3_y5[2]), .A4(ic_74273_3_y5[3]),
    .B1(ic_74240_1_z1[0]), .B2(ic_74240_1_z1[1]), .B3(ic_74240_1_z1[2]), .B4(ic_74240_1_z1[3]),
    .CIN(ic_74283_1_cout), .Y1(ic_74283_1_y1[4]), .Y2(ic_74283_1_y1[5]), .Y3(ic_74283_1_y1[6]),
    .Y4(ic_74283_1_y1[7]), .COUT(ic_74283_2_cout));
  IC_74283 ic_74283_3 (
    .A1(ic_74273_4_y1[0]), .A2(ic_74273_4_y1[1]), .A3(ic_74273_4_y1[2]), .A4(ic_74273_4_y1[3]),
    .B1(ic_74240_2_y1[0]), .B2(ic_74240_2_y1[1]), .B3(ic_74240_2_y1[2]), .B4(ic_74240_2_y1[3]),
    .CIN(ic_74283_2_cout), .Y1(ic_74283_3_y1[0]), .Y2(ic_74283_3_y1[1]), .Y3(ic_74283_3_y1[2]),
    .Y4(ic_74283_3_y1[3]), .COUT(ic_74283_3_cout));
  IC_74283 ic_74283_4 (
    .A1(ic_74273_4_y5[0]), .A2(ic_74273_4_y5[1]), .A3(ic_74273_4_y5[2]), .A4(ic_74273_4_y5[3]),
    .B1(ic_74240_2_z1[0]), .B2(ic_74240_2_z1[1]), .B3(ic_74240_2_z1[2]), .B4(ic_74240_2_z1[3]),
    .CIN(ic_74283_3_cout), .Y1(ic_74283_3_y1[4]), .Y2(ic_74283_3_y1[5]), .Y3(ic_74283_3_y1[6]),
    .Y4(ic_74283_3_y1[7]), .COUT(ic_74283_4_cout));
  // Probe on ic_74283_4_cout
  // Probe on {ic_74283_3_y1, ic_74283_1_y1}

  // Notes on the sheet:
  //   test: hw_d8_.txt
endmodule
