// Logisim project oisc_D16A16bit_hc.circ as structural Verilog: 1 circuit, main circuit main
module main (
);

  wire and_1_out, and_2_out, and_3_out, and_4_out, and_5_out, and_6_out, and_7_out, and_8_out, and_9_out,
       and_10_out, clock_1_out, comparator_1_eq, comparator_2_eq, decoder_1_out0, decoder_1_out1,
       decoder_1_out2, decoder_1_out3, decoder_1_out4, decoder_1_out5, decoder_1_out6, decoder_1_out7,
       decoder_1_out8, decoder_1_out9, decoder_1_out10, decoder_1_out11, decoder_1_out12, decoder_1_out13,
       decoder_1_out14, not_1_out, not_2_out, not_3_out, or_1_out, or_2_out, or_3_out, or_4_out, or_5_out,
       or_6_out, subtractor_1_bout, t_ff_1_q, t_ff_2_q, t_ff_3_q;
  wire [3:0] counter_1_q;
  wire [6:0] keyboard_1_data;
  wire [15:0] controlled_buffer_1_out, counter_2_q, multiplexer_2_out, portio_1_p2, register_1_q,
       register_2_q, register_3_q, subtractor_1_out;

  Clock #(.phaseOffset(1)) clock_1 (.out(clock_1_out));
  Counter #(.max('hf), .width(4)) counter_1 (.Q(counter_1_q), .clk(clock_1_out));  // open: load, D, count, carry, clr
  not not_1 (not_1_out, clock_1_out);
  Decoder #(.select(4)) decoder_1 (
    .out0(decoder_1_out0), .out1(decoder_1_out1), .out2(decoder_1_out2), .out3(decoder_1_out3),
    .out4(decoder_1_out4), .out5(decoder_1_out5), .out6(decoder_1_out6), .out7(decoder_1_out7),
    .out8(decoder_1_out8), .out9(decoder_1_out9), .out10(decoder_1_out10), .out11(decoder_1_out11),
    .out12(decoder_1_out12), .out13(decoder_1_out13), .out14(decoder_1_out14), .sel(counter_1_q));  // open: out15, en
  or or_1 (or_1_out, decoder_1_out4, decoder_1_out8, and_1_out);
  and and_1 (and_1_out, decoder_1_out13, not_1_out);
  Register #(.width(16)) register_1 (
    .D(controlled_buffer_1_out), .en(1'b1), .clk(or_2_out), .Q(register_1_q));  // open: clr
  or or_2 (or_2_out, decoder_1_out2, decoder_1_out6, decoder_1_out12);
  Keyboard keyboard_1 (.clk(and_2_out), .re(and_4_out), .data(keyboard_1_data));  // open: clr, avail
  and and_2 (and_2_out, comparator_1_eq, and_7_out);
  // PortIO #(.number(16)) portio_1: pin names not known; wires that end beside it: 1'b1, portio_1_p2
  // Probe on counter_2_q
  Counter #(.max('hffff), .width(16)) counter_2 (
    .load(and_8_out), .D(register_1_q), .Q(counter_2_q), .up(1'b1), .clk(or_1_out));  // open: count, carry, clr
  // Probe on register_1_q
  // Probe on and_8_out
  or or_3 (or_3_out, decoder_1_out3, decoder_1_out5, decoder_1_out7, decoder_1_out10);
  // Probe on portio_1_p2
  Multiplexer #(.enable("false"), .width(16)) multiplexer_1 (
    .in0(counter_2_q), .in1(register_1_q), .out(portio_1_p2), .sel(t_ff_1_q));
  T_Flip_Flop t_ff_1 (.clk(or_3_out), .T(1'b1), .Q(t_ff_1_q), .reset(decoder_1_out0));  // open: Qn, preset
  Comparator #(.mode("unsigned"), .width(16)) comparator_1 (
    .a({16{1'b1}}), .b(portio_1_p2), .eq(comparator_1_eq));  // open: gt, lt
  or or_4 (or_4_out, decoder_1_out1, decoder_1_out9, decoder_1_out11, decoder_1_out14);
  // Probe on {{9{1'b0}}, keyboard_1_data}
  T_Flip_Flop t_ff_2 (.clk(or_4_out), .T(1'b1), .Q(t_ff_2_q), .reset(decoder_1_out0));  // open: Qn, preset
  and and_3 (and_3_out, decoder_1_out9, not_1_out);
  assign controlled_buffer_1_out = and_4_out ? {{9{1'b0}}, keyboard_1_data} : 16'bz;  // Controlled_Buffer controlled_buffer_1
  and and_4 (and_4_out, t_ff_2_q, comparator_1_eq);
  and and_5 (and_5_out, t_ff_2_q, not_2_out);
  not not_2 (not_2_out, comparator_1_eq);
  and and_6 (and_6_out, and_3_out, not_3_out);
  not not_3 (not_3_out, comparator_1_eq);
  Register #(.width(16)) register_2 (
    .D(controlled_buffer_1_out), .en(1'b1), .clk(decoder_1_out8), .Q(register_2_q));  // open: clr
  T_Flip_Flop t_ff_3 (
    .clk(decoder_1_out4), .T(comparator_1_eq), .Q(t_ff_3_q), .reset(decoder_1_out0));  // open: Qn, preset
  Register #(.width(16)) register_3 (
    .D(controlled_buffer_1_out), .en(1'b1), .clk(decoder_1_out4), .Q(register_3_q));  // open: clr
  and and_7 (and_7_out, decoder_1_out4, not_1_out);
  TTY #(.cols(64), .rows(16)) tty_1 (.data(controlled_buffer_1_out[6:0]), .clk(and_10_out));  // open: we, clr
  RAM #(.addrWidth(16), .dataWidth(16), .databus("bidir"), .\type ("nonvolatile")) ram_1 (
    .addr(portio_1_p2), .data(controlled_buffer_1_out));  // open: we, oe, clk
  and and_8 (and_8_out, or_5_out, decoder_1_out13);
  // Probe on register_2_q
  // Probe on register_3_q
  // Probe on controlled_buffer_1_out
  // Probe on subtractor_1_out
  Subtractor #(.width(16)) subtractor_1 (
    .a(register_2_q), .b(register_3_q), .out(subtractor_1_out), .bout(subtractor_1_bout));  // open: bin
  // Probe on subtractor_1_bout
  Comparator #(.mode("unsigned"), .width(16)) comparator_2 (
    .a(subtractor_1_out), .b({16{1'b0}}), .eq(comparator_2_eq));  // open: gt, lt
  or or_5 (or_5_out, comparator_2_eq, subtractor_1_out[15]);
  Pull_Resistor pull_resistor_1 (.node(controlled_buffer_1_out));
  Multiplexer #(.enable("false"), .width(16)) multiplexer_2 (
    .in0(subtractor_1_out), .in1(register_3_q), .out(multiplexer_2_out), .sel(or_6_out));
  or or_6 (or_6_out, and_9_out, t_ff_3_q);
  and and_9 (and_9_out, comparator_1_eq, decoder_1_out9);
  and and_10 (and_10_out, and_9_out, not_1_out);
  assign controlled_buffer_1_out = decoder_1_out9 ? multiplexer_2_out : 16'bz;  // Controlled_Buffer controlled_buffer_2
  // PortIO #(.number(16)) portio_2: pin names not known; wires that end beside it: 1'b1, controlled_buffer_1_out

  // Notes on the sheet:
  //   read enable
  //   B_EA is 0xffff
  //   A_EA is 0xffff
  //   less equ zero
endmodule
